// Logisim project Lab 9.circ as structural Verilog
module ALU (
  input  [4:0] in_1,
  input  [31:0] A,
  input  [31:0] B,
  output NEG,
  output OVF,
  output [31:0] out_6
);

  wire and_1_out, not_1_out, not_2_out, not_3_out, or_1_out;
  wire [31:0] A_S, AND, OR, tunnel, tunnel_t, tunnel_t_t, tunnel_t_t_t, tunnel_t_t_t_t, tunnel_t_t_t_t_t, XOR;

  not not_1 (not_1_out, in_1[1]);
  not not_2 (not_2_out, in_1[4]);
  or or_1 (or_1_out, in_1[0], and_1_out);
  and and_1 (and_1_out, not_1_out, in_1[2], in_1[3], not_2_out);
  not not_3 (not_3_out, or_1_out);
  Add_Sub Add_Sub (.in_1(A), .in_2(B), .sub(not_3_out), .NEG(NEG), .OVF(OVF), .out_6(A_S));
  Multiplexer #(.select(5), .width(32), .enable("false")) multiplexer_1 (
    .in1(A_S), .in3(A_S), .in5(A_S), .in6(tunnel_t_t_t_t), .in7(A_S), .in8(A_S), .in9(A_S),
    .in10(tunnel_t_t_t), .in11(A_S), .in12(A_S), .in13(A_S), .in14(tunnel_t_t_t_t_t), .in15(A_S), .in16(XOR),
    .in17(A_S), .in18(tunnel_t), .in19(A_S), .in20(OR), .in21(A_S), .in22(tunnel), .in23(A_S), .in24(AND),
    .in25(A_S), .in26(tunnel_t_t), .in27(A_S), .in29(A_S), .in31(A_S), .out(out_6), .sel(in_1));  // open: in0, in2, in4, in28, in30
  Comparitor Comparitor (
    .Sub(A_S), .Neg(NEG), .OVF(OVF), .out_4(tunnel_t_t_t_t), .out_5(tunnel_t_t_t_t_t), .out_6(tunnel_t_t_t),
    .out_7(tunnel_t_t), .out_8(tunnel_t), .out_9(tunnel));
  XOR32 XOR_32 (.A(A), .out_3(XOR), .B(B));
  AND32 AND_32 (.in_2(A), .out_3(AND), .in_1(B));
  OR32 OR_32 (.in_2(A), .out_3(OR), .in_1(B));
endmodule

module Comparitor (
  input  [31:0] Sub,
  input  Neg,
  input  OVF,
  output [31:0] out_4,
  output [31:0] out_5,
  output [31:0] out_6,
  output [31:0] out_7,
  output [31:0] out_8,
  output [31:0] out_9
);

  wire isZero_out_2, nor_1_out, nor_2_out, not_1_out, not_2_out, not_3_out, not_4_out, not_5_out, not_6_out,
       not_7_out, not_8_out, not_9_out, not_10_out, not_11_out, or_1_out, or_2_out;

  isZero isZero (.in_1(Sub), .out_2(isZero_out_2));
  not not_1 (not_1_out, OVF);
  not not_2 (not_2_out, isZero_out_2);
  not not_3 (not_3_out, Neg);
  not not_4 (not_4_out, OVF);
  not not_5 (not_5_out, isZero_out_2);
  not not_6 (not_6_out, isZero_out_2);
  not not_7 (not_7_out, Neg);
  not not_8 (not_8_out, isZero_out_2);
  nor nor_1 (nor_1_out, isZero_out_2, Neg);
  not not_9 (not_9_out, Neg);
  or or_1 (or_1_out, not_9_out, isZero_out_2);
  or or_2 (or_2_out, Neg, isZero_out_2);
  nor nor_2 (nor_2_out, isZero_out_2, not_10_out);
  not not_10 (not_10_out, Neg);
  // AND_Gate and_1 has open pins: in0=not_1_out, in1=not_2_out, in2=not_3_out, out=open
  // AND_Gate and_2 has open pins: in0=not_4_out, in1=not_5_out, in2=Neg, out=open
  // AND_Gate and_3 has open pins: in0=OVF, in1=not_6_out, in2=not_7_out, out=open
  // AND_Gate and_4 has open pins: in0=OVF, in1=not_8_out, in2=Neg, out=open
  make32 make32_1 (.in_1(nor_1_out), .out_2(out_4));
  make32 make32_2 (.in_1(or_1_out), .out_2(out_5));
  make32 make32_3 (.in_1(isZero_out_2), .out_2(out_6));
  make32 make32_4 (.in_1(or_2_out), .out_2(out_7));
  make32 make32_5 (.in_1(nor_2_out), .out_2(out_8));
  make32 make32_6 (.in_1(not_11_out), .out_2(out_9));
  not not_11 (not_11_out, isZero_out_2);
endmodule

module isZero (
  input  [31:0] in_1,
  output out_2
);

  nor nor_1 (out_2, in_1[0], in_1[1], in_1[2], in_1[3], in_1[4], in_1[5], in_1[6], in_1[7], in_1[8], in_1[9], in_1[10], in_1[11], in_1[12], in_1[13], in_1[14], in_1[15], in_1[16], in_1[17], in_1[18], in_1[19], in_1[20], in_1[21], in_1[22], in_1[23], in_1[24], in_1[25], in_1[26], in_1[27], in_1[28], in_1[29], in_1[30], in_1[31]);
endmodule

module make32 (
  input  in_1,
  output [31:0] out_2
);


  assign out_2 = {{31{1'b0}}, in_1};
endmodule

module Shifter (
  input  shift,
  input  right,
  input  [4:0] in_3,
  input  [31:0] in_4,
  output [31:0] out_5
);

  wire [31:0] shifter_1_out, shifter_2_out;

  Shifter_part #(.width(32)) shifter_1 (.in(in_4), .\dist (in_3), .out(shifter_1_out));
  Shifter_part #(.width(32), .shift("lr")) shifter_2 (.in(in_4), .\dist (in_3), .out(shifter_2_out));
  Multiplexer #(.select(2), .width(32), .enable("false")) multiplexer_1 (
    .in0(in_4), .in1(in_4), .in2(shifter_1_out), .in3(shifter_2_out), .out(out_5), .sel({shift, right}));
endmodule

module IR (
  input  [31:0] DI_31_0,
  input  I_type,
  input  J_Link,
  output [4:0] Aaddr,
  output [4:0] Baddr,
  output [4:0] Caddr,
  output [31:0] Inst,
  output [31:0] Imm
);

  wire [4:0] multiplexer_1_out;

  Multiplexer #(.width(5), .enable("false")) multiplexer_1 (
    .in0(DI_31_0[15:11]), .in1(DI_31_0[20:16]), .out(multiplexer_1_out), .sel(I_type));
  assign Imm = {{16{1'b0}}, DI_31_0[15:0]};  // Bit_Extender bit_extender_1
  Multiplexer #(.width(5), .enable("false")) multiplexer_2 (
    .in0(multiplexer_1_out), .in1({5{1'b1}}), .out(Caddr), .sel(J_Link));

  assign Aaddr = DI_31_0[25:21];
  assign Baddr = DI_31_0[20:16];
  assign Inst = DI_31_0;
endmodule

module PC (
  input  [31:0] Imm,
  input  btaken,
  input  [31:0] Imm_2,
  input  btaken_2,
  output [31:0] out_5,
  output [31:0] out_6
);

  wire clock_1_out, clock_2_out;
  wire [31:0] adder_1_out, adder_2_out, multiplexer_1_out, PC_2_q, PC_q;

  Clock clock_1 (.out(clock_1_out));
  Register #(.width(32)) PC (.D(out_5), .Q(PC_q), .clk(clock_1_out));  // open: en, clr
  Register #(.width(32)) PC_2 (.D(out_6), .Q(PC_2_q), .clk(clock_2_out));  // open: en, clr
  Clock clock_2 (.out(clock_2_out));
  Adder #(.width(32)) adder_1 (.a(32'h1), .b(PC_q), .out(adder_1_out));  // open: cin, cout
  Adder #(.width(32)) adder_2 (.a(adder_1_out), .b(Imm), .out(adder_2_out));  // open: cin, cout
  Multiplexer #(.width(32), .enable("false")) multiplexer_1 (
    .in0(32'h1), .in1(Imm_2), .out(multiplexer_1_out), .sel(btaken_2));
  Multiplexer #(.width(32), .enable("false")) multiplexer_2 (
    .in0(adder_1_out), .in1(adder_2_out), .out(out_5), .sel(btaken));
  Adder #(.width(32)) adder_3 (.a(PC_2_q), .b(multiplexer_1_out), .out(out_6));  // open: cin, cout
endmodule
