// Logisim project Lab6.circ as structural Verilog: 10 circuits, main circuit main
module main (
);

  Multiplexer #(.enable("false")) multiplexer_1 ();  // open: in0, in1, out, sel
endmodule

module Task2Partf (
  input  A,
  input  B,
  input  C,
  output Out1,
  output Out2
);

  wire A_AND_B_out, A_AND_C_out, B_AND_C_out, xor_1_out;

  and A_AND_B (A_AND_B_out, A, B);
  and A_AND_C (A_AND_C_out, A, C);
  and B_AND_C (B_AND_C_out, B, C);
  xor xor_1 (xor_1_out, A, B);
  or or_1 (Out1, A_AND_B_out, A_AND_C_out, B_AND_C_out);
  xor xor_2 (Out2, xor_1_out, C);

  // Notes on the sheet:
  //   C
endmodule

module A_4 (
  input  in_1,
  input  in_2,
  input  in_3,
  input  in_4,
  input  in_5,
  output out_6,
  output out_7,
  output out_8
);

  wire task2partf_1_out1, task2partf_2_out1, task2partf_2_out2, task2partf_3_out1, task2partf_3_out2;

  Task2Partf task2partf_1 (.A(in_1), .B(in_2), .C(in_3), .Out1(task2partf_1_out1), .Out2(out_8));
  Task2Partf task2partf_2 (.A(1'b0), .B(in_4), .C(in_5), .Out1(task2partf_2_out1), .Out2(task2partf_2_out2));
  Task2Partf task2partf_3 (.A(1'b1), .B(in_4), .C(in_5), .Out1(task2partf_3_out1), .Out2(task2partf_3_out2));
  Multiplexer #(.enable("false")) multiplexer_1 (
    .in0(task2partf_2_out1), .in1(task2partf_3_out1), .out(out_6), .sel(task2partf_1_out1));
  Multiplexer #(.enable("false")) multiplexer_2 (
    .in0(task2partf_2_out2), .in1(task2partf_3_out2), .out(out_7), .sel(task2partf_1_out1));
endmodule

module A_8 (
  input  in_1,
  input  in_2,
  input  in_3,
  input  in_4,
  input  in_5,
  input  in_6,
  input  in_7,
  input  in_8,
  input  in_9,
  output _1,
  output _2,
  output _3,
  output _4,
  output _5
);

  wire a_4_1_out_6, a_4_2_out_6, a_4_2_out_7, a_4_2_out_8, a_4_3_out_6, a_4_3_out_7, a_4_3_out_8;

  A_4 a_4_1 (
    .in_1(in_1), .in_2(in_2), .in_3(in_3), .in_4(in_4), .in_5(in_5), .out_6(a_4_1_out_6), .out_7(_2),
    .out_8(_1));
  A_4 a_4_2 (
    .in_1(1'b0), .in_2(in_6), .in_3(in_7), .in_4(in_8), .in_5(in_9), .out_6(a_4_2_out_6),
    .out_7(a_4_2_out_7), .out_8(a_4_2_out_8));
  A_4 a_4_3 (
    .in_1(1'b1), .in_2(in_6), .in_3(in_7), .in_4(in_8), .in_5(in_9), .out_6(a_4_3_out_6),
    .out_7(a_4_3_out_7), .out_8(a_4_3_out_8));
  Multiplexer #(.enable("false")) multiplexer_1 (.in0(a_4_2_out_6), .in1(a_4_3_out_6), .out(_5), .sel(a_4_1_out_6));
  Multiplexer #(.enable("false")) multiplexer_2 (.in0(a_4_2_out_7), .in1(a_4_3_out_7), .out(_4), .sel(a_4_1_out_6));
  Multiplexer #(.enable("false")) multiplexer_3 (.in0(a_4_2_out_8), .in1(a_4_3_out_8), .out(_3), .sel(a_4_1_out_6));
endmodule

module A_16 (
  input  in_1,
  input  in_2,
  input  in_3,
  input  in_4,
  input  in_5,
  input  in_6,
  input  in_7,
  input  in_8,
  input  in_9,
  input  in_10,
  input  in_11,
  input  in_12,
  input  in_13,
  input  in_14,
  input  in_15,
  input  in_16,
  input  in_17,
  output out_18,
  output out_19,
  output out_20,
  output out_21,
  output out_22,
  output out_23,
  output out_24,
  output out_25,
  output out_26
);

  wire a_8_1__5, a_8_2__1, a_8_2__2, a_8_2__3, a_8_2__4, a_8_2__5, a_8_3__1, a_8_3__2, a_8_3__3, a_8_3__4,
       a_8_3__5;

  A_8 a_8_1 (
    .in_1(in_1), .in_2(in_2), .in_3(in_3), .in_4(in_4), .in_5(in_5), .in_6(in_6), .in_7(in_7), .in_8(in_8),
    .in_9(in_9), ._1(out_18), ._2(out_19), ._3(out_20), ._4(out_21), ._5(a_8_1__5));
  A_8 a_8_2 (
    .in_1(1'b0), .in_2(in_10), .in_3(in_11), .in_4(in_12), .in_5(in_13), .in_6(in_14), .in_7(in_15),
    .in_8(in_16), .in_9(in_17), ._1(a_8_2__1), ._2(a_8_2__2), ._3(a_8_2__3), ._4(a_8_2__4), ._5(a_8_2__5));
  A_8 a_8_3 (
    .in_1(1'b1), .in_2(in_10), .in_3(in_11), .in_4(in_12), .in_5(in_13), .in_6(in_14), .in_7(in_15),
    .in_8(in_16), .in_9(in_17), ._1(a_8_3__1), ._2(a_8_3__2), ._3(a_8_3__3), ._4(a_8_3__4), ._5(a_8_3__5));
  Multiplexer #(.enable("false")) multiplexer_1 (.in0(a_8_2__1), .in1(a_8_3__1), .out(out_22), .sel(a_8_1__5));
  Multiplexer #(.enable("false")) multiplexer_2 (.in0(a_8_2__2), .in1(a_8_3__2), .out(out_23), .sel(a_8_1__5));
  Multiplexer #(.enable("false")) multiplexer_3 (.in0(a_8_2__3), .in1(a_8_3__3), .out(out_24), .sel(a_8_1__5));
  Multiplexer #(.enable("false")) multiplexer_4 (.in0(a_8_2__4), .in1(a_8_3__4), .out(out_25), .sel(a_8_1__5));
  Multiplexer #(.enable("false")) multiplexer_5 (.in0(a_8_2__5), .in1(a_8_3__5), .out(out_26), .sel(a_8_1__5));
endmodule

module A_32 (
  input  in_1,
  input  [15:0] in_2,
  input  [15:0] in_3,
  output out_4,
  output out_5,
  output out_6,
  output out_7,
  output out_8,
  output out_9,
  output out_10,
  output out_11,
  output out_12,
  output out_13,
  output out_14,
  output out_15,
  output out_16,
  output out_17,
  output out_18,
  output out_19,
  output out_20
);

  wire a_16_1_out_26, a_16_2_out_18, a_16_2_out_19, a_16_2_out_20, a_16_2_out_21, a_16_2_out_22,
       a_16_2_out_23, a_16_2_out_24, a_16_2_out_25, a_16_2_out_26, a_16_3_out_18, a_16_3_out_19,
       a_16_3_out_20, a_16_3_out_21, a_16_3_out_22, a_16_3_out_23, a_16_3_out_24, a_16_3_out_25,
       a_16_3_out_26;

  A_16 a_16_1 (
    .in_1(in_1), .in_2(in_3[0]), .in_3(in_2[0]), .in_4(in_3[1]), .in_5(in_2[1]), .in_6(in_3[2]),
    .in_7(in_2[2]), .in_8(in_3[3]), .in_9(in_2[3]), .in_10(in_3[4]), .in_11(in_2[4]), .in_12(in_3[5]),
    .in_13(in_2[5]), .in_14(in_3[6]), .in_15(in_2[6]), .in_16(in_3[7]), .in_17(in_2[7]), .out_18(out_4),
    .out_19(out_5), .out_20(out_6), .out_21(out_7), .out_22(out_8), .out_23(out_9), .out_24(out_10),
    .out_25(out_11), .out_26(a_16_1_out_26));
  A_16 a_16_2 (
    .in_1(1'b0), .in_2(in_2[8]), .in_3(in_3[8]), .in_4(in_2[9]), .in_5(in_3[9]), .in_6(in_2[10]),
    .in_7(in_3[10]), .in_8(in_2[11]), .in_9(in_3[11]), .in_10(in_2[12]), .in_11(in_3[12]), .in_12(in_2[13]),
    .in_13(in_3[13]), .in_14(in_2[14]), .in_15(in_3[14]), .in_16(in_2[15]), .in_17(in_3[15]),
    .out_18(a_16_2_out_18), .out_19(a_16_2_out_19), .out_20(a_16_2_out_20), .out_21(a_16_2_out_21),
    .out_22(a_16_2_out_22), .out_23(a_16_2_out_23), .out_24(a_16_2_out_24), .out_25(a_16_2_out_25),
    .out_26(a_16_2_out_26));
  A_16 a_16_3 (
    .in_1(1'b1), .in_2(in_2[8]), .in_3(in_3[8]), .in_4(in_2[9]), .in_5(in_3[9]), .in_6(in_2[10]),
    .in_7(in_3[10]), .in_8(in_2[11]), .in_9(in_3[11]), .in_10(in_2[12]), .in_11(in_3[12]), .in_12(in_2[13]),
    .in_13(in_3[13]), .in_14(in_2[14]), .in_15(in_3[14]), .in_16(in_2[15]), .in_17(in_3[15]),
    .out_18(a_16_3_out_18), .out_19(a_16_3_out_19), .out_20(a_16_3_out_20), .out_21(a_16_3_out_21),
    .out_22(a_16_3_out_22), .out_23(a_16_3_out_23), .out_24(a_16_3_out_24), .out_25(a_16_3_out_25),
    .out_26(a_16_3_out_26));
  Multiplexer #(.enable("false")) multiplexer_1 (
    .in0(a_16_2_out_18), .in1(a_16_3_out_18), .out(out_12), .sel(a_16_1_out_26));
  Multiplexer #(.enable("false")) multiplexer_2 (
    .in0(a_16_2_out_19), .in1(a_16_3_out_19), .out(out_13), .sel(a_16_1_out_26));
  Multiplexer #(.enable("false")) multiplexer_3 (
    .in0(a_16_2_out_20), .in1(a_16_3_out_20), .out(out_14), .sel(a_16_1_out_26));
  Multiplexer #(.enable("false")) multiplexer_4 (
    .in0(a_16_2_out_21), .in1(a_16_3_out_21), .out(out_15), .sel(a_16_1_out_26));
  Multiplexer #(.enable("false")) multiplexer_5 (
    .in0(a_16_2_out_22), .in1(a_16_3_out_22), .out(out_16), .sel(a_16_1_out_26));
  Multiplexer #(.enable("false")) multiplexer_6 (
    .in0(a_16_2_out_23), .in1(a_16_3_out_23), .out(out_17), .sel(a_16_1_out_26));
  Multiplexer #(.enable("false")) multiplexer_7 (
    .in0(a_16_2_out_24), .in1(a_16_3_out_24), .out(out_18), .sel(a_16_1_out_26));
  Multiplexer #(.enable("false")) multiplexer_8 (
    .in0(a_16_2_out_25), .in1(a_16_3_out_25), .out(out_19), .sel(a_16_1_out_26));
  Multiplexer #(.enable("false")) multiplexer_9 (
    .in0(a_16_2_out_26), .in1(a_16_3_out_26), .out(out_20), .sel(a_16_1_out_26));
endmodule

module Part2 (
);

  wire [3:0] joystick_1_x, joystick_1_y;
  wire [15:0] decoder_1_out15, demultiplexer_1_out0, demultiplexer_1_out1, demultiplexer_1_out2,
       demultiplexer_1_out3, demultiplexer_1_out4, demultiplexer_1_out5, demultiplexer_1_out6,
       demultiplexer_1_out7, demultiplexer_1_out8, demultiplexer_1_out9, demultiplexer_1_out10,
       demultiplexer_1_out11, demultiplexer_1_out12, demultiplexer_1_out13, demultiplexer_1_out14,
       demultiplexer_1_out15;

  Hex_Digit_Display hex_digit_display_1 (.value(joystick_1_x));  // open: dp
  Joystick joystick_1 (.x(joystick_1_x), .y(joystick_1_y));
  Hex_Digit_Display hex_digit_display_2 (.value(joystick_1_y));  // open: dp
  DotMatrix #(.matrixcols(16), .matrixrows(16)) dotmatrix_1 (
    .col0(demultiplexer_1_out0), .col1(demultiplexer_1_out1), .col2(demultiplexer_1_out2),
    .col3(demultiplexer_1_out3), .col4(demultiplexer_1_out4), .col5(demultiplexer_1_out5),
    .col6(demultiplexer_1_out6), .col7(demultiplexer_1_out7), .col8(demultiplexer_1_out8),
    .col9(demultiplexer_1_out9), .col10(demultiplexer_1_out10), .col11(demultiplexer_1_out11),
    .col12(demultiplexer_1_out12), .col13(demultiplexer_1_out13), .col14(demultiplexer_1_out14),
    .col15(demultiplexer_1_out15));
  Decoder #(.select(4), .enable("false")) decoder_1 (
    .out0(decoder_1_out15[15]), .out1(decoder_1_out15[14]), .out2(decoder_1_out15[13]),
    .out3(decoder_1_out15[12]), .out4(decoder_1_out15[11]), .out5(decoder_1_out15[10]),
    .out6(decoder_1_out15[9]), .out7(decoder_1_out15[8]), .out8(decoder_1_out15[7]),
    .out9(decoder_1_out15[6]), .out10(decoder_1_out15[5]), .out11(decoder_1_out15[4]),
    .out12(decoder_1_out15[3]), .out13(decoder_1_out15[2]), .out14(decoder_1_out15[1]),
    .out15(decoder_1_out15[0]), .sel(joystick_1_y));
  Demultiplexer #(.select(4), .width(16), .enable("false")) demultiplexer_1 (
    .out0(demultiplexer_1_out0), .out1(demultiplexer_1_out1), .out2(demultiplexer_1_out2),
    .out3(demultiplexer_1_out3), .out4(demultiplexer_1_out4), .out5(demultiplexer_1_out5),
    .out6(demultiplexer_1_out6), .out7(demultiplexer_1_out7), .out8(demultiplexer_1_out8),
    .out9(demultiplexer_1_out9), .out10(demultiplexer_1_out10), .out11(demultiplexer_1_out11),
    .out12(demultiplexer_1_out12), .out13(demultiplexer_1_out13), .out14(demultiplexer_1_out14),
    .out15(demultiplexer_1_out15), .in(decoder_1_out15), .sel(joystick_1_x));
endmodule

module Part2B (
);

  wire [3:0] joystick_1_x, joystick_1_y;
  wire [15:0] decoder_1_out15, demultiplexer_1_out0, demultiplexer_1_out1, demultiplexer_1_out2,
       demultiplexer_1_out3, demultiplexer_1_out4, demultiplexer_1_out5, demultiplexer_1_out6,
       demultiplexer_1_out7, demultiplexer_1_out8, demultiplexer_1_out9, demultiplexer_1_out10,
       demultiplexer_1_out11, demultiplexer_1_out12, demultiplexer_1_out13, demultiplexer_1_out14,
       demultiplexer_1_out15, part2b_orgates_1_out_17, part2b_orgates_1_out_18, part2b_orgates_1_out_19,
       part2b_orgates_1_out_20, part2b_orgates_1_out_21, part2b_orgates_1_out_22, part2b_orgates_1_out_23,
       part2b_orgates_1_out_24, part2b_orgates_1_out_25, part2b_orgates_1_out_26, part2b_orgates_1_out_27,
       part2b_orgates_1_out_28, part2b_orgates_1_out_29, part2b_orgates_1_out_30, part2b_orgates_1_out_31,
       part2b_orgates_1_out_32;

  Joystick joystick_1 (.x(joystick_1_x), .y(joystick_1_y));
  Hex_Digit_Display hex_digit_display_1 (.value(joystick_1_x));  // open: dp
  Hex_Digit_Display hex_digit_display_2 (.value(joystick_1_y));  // open: dp
  DotMatrix #(.matrixcols(16), .matrixrows(16)) dotmatrix_1 (
    .col0(part2b_orgates_1_out_27), .col1(part2b_orgates_1_out_20), .col2(part2b_orgates_1_out_25),
    .col3(part2b_orgates_1_out_21), .col4(part2b_orgates_1_out_26), .col5(part2b_orgates_1_out_17),
    .col6(part2b_orgates_1_out_28), .col7(part2b_orgates_1_out_22), .col8(part2b_orgates_1_out_29),
    .col9(part2b_orgates_1_out_18), .col10(part2b_orgates_1_out_30), .col11(part2b_orgates_1_out_23),
    .col12(part2b_orgates_1_out_31), .col13(part2b_orgates_1_out_24), .col14(part2b_orgates_1_out_32),
    .col15(part2b_orgates_1_out_19));
  Part2B_ORgates part2b_orgates_1 (
    .out_27(part2b_orgates_1_out_27), .out_20(part2b_orgates_1_out_20), .out_25(part2b_orgates_1_out_25),
    .out_21(part2b_orgates_1_out_21), .out_26(part2b_orgates_1_out_26), .out_17(part2b_orgates_1_out_17),
    .out_28(part2b_orgates_1_out_28), .out_22(part2b_orgates_1_out_22), .out_29(part2b_orgates_1_out_29),
    .out_18(part2b_orgates_1_out_18), .out_30(part2b_orgates_1_out_30), .out_23(part2b_orgates_1_out_23),
    .out_31(part2b_orgates_1_out_31), .out_24(part2b_orgates_1_out_24), .out_32(part2b_orgates_1_out_32),
    .out_19(part2b_orgates_1_out_19), .in_1(demultiplexer_1_out0), .in_9(demultiplexer_1_out1),
    .in_2(demultiplexer_1_out2), .in_10(demultiplexer_1_out3), .in_3(demultiplexer_1_out4),
    .in_11(demultiplexer_1_out5), .in_4(demultiplexer_1_out6), .in_12(demultiplexer_1_out7),
    .in_5(demultiplexer_1_out8), .in_13(demultiplexer_1_out9), .in_6(demultiplexer_1_out10),
    .in_14(demultiplexer_1_out11), .in_7(demultiplexer_1_out12), .in_15(demultiplexer_1_out13),
    .in_8(demultiplexer_1_out14), .in_16(demultiplexer_1_out15));
  Decoder #(.select(4), .enable("false")) decoder_1 (
    .out0(decoder_1_out15[15]), .out1(decoder_1_out15[14]), .out2(decoder_1_out15[13]),
    .out3(decoder_1_out15[12]), .out4(decoder_1_out15[11]), .out5(decoder_1_out15[10]),
    .out6(decoder_1_out15[9]), .out7(decoder_1_out15[8]), .out8(decoder_1_out15[7]),
    .out9(decoder_1_out15[6]), .out10(decoder_1_out15[5]), .out11(decoder_1_out15[4]),
    .out12(decoder_1_out15[3]), .out13(decoder_1_out15[2]), .out14(decoder_1_out15[1]),
    .out15(decoder_1_out15[0]), .sel(joystick_1_y));
  Demultiplexer #(.select(4), .width(16), .enable("false")) demultiplexer_1 (
    .out0(demultiplexer_1_out0), .out1(demultiplexer_1_out1), .out2(demultiplexer_1_out2),
    .out3(demultiplexer_1_out3), .out4(demultiplexer_1_out4), .out5(demultiplexer_1_out5),
    .out6(demultiplexer_1_out6), .out7(demultiplexer_1_out7), .out8(demultiplexer_1_out8),
    .out9(demultiplexer_1_out9), .out10(demultiplexer_1_out10), .out11(demultiplexer_1_out11),
    .out12(demultiplexer_1_out12), .out13(demultiplexer_1_out13), .out14(demultiplexer_1_out14),
    .out15(demultiplexer_1_out15), .in(decoder_1_out15), .sel(joystick_1_x));
endmodule

module Part2B_ORgates (
  input  [15:0] in_1,
  input  [15:0] in_2,
  input  [15:0] in_3,
  input  [15:0] in_4,
  input  [15:0] in_5,
  input  [15:0] in_6,
  input  [15:0] in_7,
  input  [15:0] in_8,
  input  [15:0] in_9,
  input  [15:0] in_10,
  input  [15:0] in_11,
  input  [15:0] in_12,
  input  [15:0] in_13,
  input  [15:0] in_14,
  input  [15:0] in_15,
  input  [15:0] in_16,
  output [15:0] out_17,
  output [15:0] out_18,
  output [15:0] out_19,
  output [15:0] out_20,
  output [15:0] out_21,
  output [15:0] out_22,
  output [15:0] out_23,
  output [15:0] out_24,
  output [15:0] out_25,
  output [15:0] out_26,
  output [15:0] out_27,
  output [15:0] out_28,
  output [15:0] out_29,
  output [15:0] out_30,
  output [15:0] out_31,
  output [15:0] out_32
);

  assign out_27 = in_1 | in_9;  // OR_Gate or_1, 16 bits wide
  assign out_20 = in_9 | in_2;  // OR_Gate or_2, 16 bits wide
  assign out_21 = in_10 | in_3;  // OR_Gate or_3, 16 bits wide
  assign out_25 = in_2 | in_10;  // OR_Gate or_4, 16 bits wide
  assign out_26 = in_3 | in_11;  // OR_Gate or_5, 16 bits wide
  assign out_17 = in_11 | in_4;  // OR_Gate or_6, 16 bits wide
  assign out_28 = in_4 | in_12;  // OR_Gate or_7, 16 bits wide
  assign out_29 = in_5 | in_13;  // OR_Gate or_8, 16 bits wide
  assign out_22 = in_12 | in_5;  // OR_Gate or_9, 16 bits wide
  assign out_18 = in_13 | in_6;  // OR_Gate or_10, 16 bits wide
  assign out_30 = in_6 | in_14;  // OR_Gate or_11, 16 bits wide
  assign out_31 = in_7 | in_15;  // OR_Gate or_12, 16 bits wide
  assign out_23 = in_14 | in_7;  // OR_Gate or_13, 16 bits wide
  assign out_24 = in_15 | in_8;  // OR_Gate or_14, 16 bits wide
  assign out_32 = in_8 | in_16;  // OR_Gate or_15, 16 bits wide
  assign out_19 = in_16;  // OR_Gate or_16, 16 bits wide OR_Gate
endmodule

module Part2C (
);

  wire [4:0] joystick_1_x, joystick_1_y;
  wire [31:0] decoder_1_out31, demultiplexer_1_out0, demultiplexer_1_out1, demultiplexer_1_out2,
       demultiplexer_1_out3, demultiplexer_1_out4, demultiplexer_1_out5, demultiplexer_1_out6,
       demultiplexer_1_out7, demultiplexer_1_out8, demultiplexer_1_out9, demultiplexer_1_out10,
       demultiplexer_1_out11, demultiplexer_1_out12, demultiplexer_1_out13, demultiplexer_1_out14,
       demultiplexer_1_out15, demultiplexer_1_out16, demultiplexer_1_out17, demultiplexer_1_out18,
       demultiplexer_1_out19, demultiplexer_1_out20, demultiplexer_1_out21, demultiplexer_1_out22,
       demultiplexer_1_out23, demultiplexer_1_out24, demultiplexer_1_out25, demultiplexer_1_out26,
       demultiplexer_1_out27, demultiplexer_1_out28, demultiplexer_1_out29, demultiplexer_1_out30,
       demultiplexer_1_out31;

  Joystick #(.bits(5)) joystick_1 (.x(joystick_1_x), .y(joystick_1_y));
  DotMatrix #(.matrixcols(32), .matrixrows(32)) dotmatrix_1 (
    .col0(demultiplexer_1_out0), .col1(demultiplexer_1_out1), .col2(demultiplexer_1_out2),
    .col3(demultiplexer_1_out3), .col4(demultiplexer_1_out4), .col5(demultiplexer_1_out5),
    .col6(demultiplexer_1_out6), .col7(demultiplexer_1_out7), .col8(demultiplexer_1_out8),
    .col9(demultiplexer_1_out9), .col10(demultiplexer_1_out10), .col11(demultiplexer_1_out11),
    .col12(demultiplexer_1_out12), .col13(demultiplexer_1_out13), .col14(demultiplexer_1_out14),
    .col15(demultiplexer_1_out15), .col16(demultiplexer_1_out16), .col17(demultiplexer_1_out17),
    .col18(demultiplexer_1_out18), .col19(demultiplexer_1_out19), .col20(demultiplexer_1_out20),
    .col21(demultiplexer_1_out21), .col22(demultiplexer_1_out22), .col23(demultiplexer_1_out23),
    .col24(demultiplexer_1_out24), .col25(demultiplexer_1_out25), .col26(demultiplexer_1_out26),
    .col27(demultiplexer_1_out27), .col28(demultiplexer_1_out28), .col29(demultiplexer_1_out29),
    .col30(demultiplexer_1_out30), .col31(demultiplexer_1_out31));
  Decoder #(.select(5), .enable("false")) decoder_1 (
    .out0(decoder_1_out31[31]), .out1(decoder_1_out31[30]), .out2(decoder_1_out31[29]),
    .out3(decoder_1_out31[28]), .out4(decoder_1_out31[27]), .out5(decoder_1_out31[26]),
    .out6(decoder_1_out31[25]), .out7(decoder_1_out31[24]), .out8(decoder_1_out31[23]),
    .out9(decoder_1_out31[22]), .out10(decoder_1_out31[21]), .out11(decoder_1_out31[20]),
    .out12(decoder_1_out31[19]), .out13(decoder_1_out31[18]), .out14(decoder_1_out31[17]),
    .out15(decoder_1_out31[16]), .out16(decoder_1_out31[15]), .out17(decoder_1_out31[14]),
    .out18(decoder_1_out31[13]), .out19(decoder_1_out31[12]), .out20(decoder_1_out31[11]),
    .out21(decoder_1_out31[10]), .out22(decoder_1_out31[9]), .out23(decoder_1_out31[8]),
    .out24(decoder_1_out31[7]), .out25(decoder_1_out31[6]), .out26(decoder_1_out31[5]),
    .out27(decoder_1_out31[4]), .out28(decoder_1_out31[3]), .out29(decoder_1_out31[2]),
    .out30(decoder_1_out31[1]), .out31(decoder_1_out31[0]), .sel(joystick_1_y));
  Demultiplexer #(.select(5), .width(32), .enable("false")) demultiplexer_1 (
    .out0(demultiplexer_1_out0), .out1(demultiplexer_1_out1), .out2(demultiplexer_1_out2),
    .out3(demultiplexer_1_out3), .out4(demultiplexer_1_out4), .out5(demultiplexer_1_out5),
    .out6(demultiplexer_1_out6), .out7(demultiplexer_1_out7), .out8(demultiplexer_1_out8),
    .out9(demultiplexer_1_out9), .out10(demultiplexer_1_out10), .out11(demultiplexer_1_out11),
    .out12(demultiplexer_1_out12), .out13(demultiplexer_1_out13), .out14(demultiplexer_1_out14),
    .out15(demultiplexer_1_out15), .out16(demultiplexer_1_out16), .out17(demultiplexer_1_out17),
    .out18(demultiplexer_1_out18), .out19(demultiplexer_1_out19), .out20(demultiplexer_1_out20),
    .out21(demultiplexer_1_out21), .out22(demultiplexer_1_out22), .out23(demultiplexer_1_out23),
    .out24(demultiplexer_1_out24), .out25(demultiplexer_1_out25), .out26(demultiplexer_1_out26),
    .out27(demultiplexer_1_out27), .out28(demultiplexer_1_out28), .out29(demultiplexer_1_out29),
    .out30(demultiplexer_1_out30), .out31(demultiplexer_1_out31), .in(decoder_1_out31), .sel(joystick_1_x));
endmodule
