// Logisim project Lab7.circ as structural Verilog
module S_Adder (
  input  [31:0] A,
  input  [31:0] B,
  input  C_0,
  output Neg,
  output OVF,
  output C_n,
  output out_7,
  output out_8,
  output out_9,
  output out_10,
  output out_11,
  output out_12,
  output out_13,
  output out_14,
  output out_15,
  output out_16,
  output out_17,
  output out_18,
  output out_19,
  output out_20,
  output out_21,
  output out_22,
  output out_23,
  output out_24,
  output out_25,
  output out_26,
  output out_27,
  output out_28,
  output out_29,
  output out_30,
  output out_31,
  output out_32,
  output out_33,
  output out_34,
  output out_35,
  output out_36,
  output out_37,
  output out_38
);

  XOR3 xor3_1 (.A(A), .B(B), .C_n(C_n), .out_4(Neg));
  XOR_XOR4 xor_xor4_1 (.A(A), .B(B), .S_n_1(out_7), .C_n(C_n), .out_5(OVF));
  Adder32 Adder (
    .in_1(C_0), .in_2(B), .in_3(A), .out_4(out_38), .out_5(out_37), .out_6(out_36), .out_7(out_35),
    .out_8(out_34), .out_9(out_33), .out_10(out_32), .out_11(out_31), .out_12(out_30), .out_13(out_29),
    .out_14(out_28), .out_15(out_27), .out_16(out_26), .out_17(out_25), .out_18(out_24), .out_19(out_23),
    .out_20(out_22), .out_21(out_21), .out_22(out_20), .out_23(out_19), .out_24(out_18), .out_25(out_17),
    .out_26(out_16), .out_27(out_15), .out_28(out_14), .out_29(out_13), .out_30(out_12), .out_31(out_11),
    .out_32(out_10), .out_33(out_9), .out_34(out_8), .out_35(out_7), .out_36(C_n));
endmodule

module XOR3 (
  input  [31:0] A,
  input  [31:0] B,
  input  C_n,
  output out_4
);

  wire xor_1_out;

  xor xor_1 (xor_1_out, A[31], B[31]);
  xor xor_2 (out_4, xor_1_out, C_n);
endmodule

module XOR_XOR4 (
  input  C_n,
  input  S_n_1,
  input  [31:0] A,
  input  [31:0] B,
  output out_5
);

  wire xor_1_out, xor_2_out;

  xor xor_1 (xor_1_out, A[31], B[31]);
  xor xor_2 (xor_2_out, xor_1_out, C_n);
  xor xor_3 (out_5, xor_2_out, S_n_1);
endmodule

module Adder32 (
  input  in_1,
  input  [31:0] in_2,
  input  [31:0] in_3,
  output out_4,
  output out_5,
  output out_6,
  output out_7,
  output out_8,
  output out_9,
  output out_10,
  output out_11,
  output out_12,
  output out_13,
  output out_14,
  output out_15,
  output out_16,
  output out_17,
  output out_18,
  output out_19,
  output out_20,
  output out_21,
  output out_22,
  output out_23,
  output out_24,
  output out_25,
  output out_26,
  output out_27,
  output out_28,
  output out_29,
  output out_30,
  output out_31,
  output out_32,
  output out_33,
  output out_34,
  output out_35,
  output out_36
);

  wire _1, _2, _3, _4, _5, _6, _7, _8, _9, _10, _11, _12, _13, _14, _15, _16, _17, a_32_1_out_4,
       a_32_1_out_5, a_32_1_out_6, a_32_1_out_7, a_32_1_out_8, a_32_1_out_9, a_32_1_out_10, a_32_1_out_11,
       a_32_1_out_12, a_32_1_out_13, a_32_1_out_14, a_32_1_out_15, a_32_1_out_16, a_32_1_out_17,
       a_32_1_out_18, a_32_1_out_19, a_32_1_out_20, C;

  A_32 a_32_1 (
    .in_1(1'b0), .in_2(in_2[31:16]), .in_3(in_3[31:16]), .out_4(a_32_1_out_4), .out_5(a_32_1_out_5),
    .out_6(a_32_1_out_6), .out_7(a_32_1_out_7), .out_8(a_32_1_out_8), .out_9(a_32_1_out_9),
    .out_10(a_32_1_out_10), .out_11(a_32_1_out_11), .out_12(a_32_1_out_12), .out_13(a_32_1_out_13),
    .out_14(a_32_1_out_14), .out_15(a_32_1_out_15), .out_16(a_32_1_out_16), .out_17(a_32_1_out_17),
    .out_18(a_32_1_out_18), .out_19(a_32_1_out_19), .out_20(a_32_1_out_20));
  A_32 a_32_2 (
    .in_1(1'b1), .in_2(in_2[31:16]), .in_3(in_3[31:16]), .out_4(_1), .out_5(_2), .out_6(_3), .out_7(_4),
    .out_8(_5), .out_9(_6), .out_10(_7), .out_11(_8), .out_12(_9), .out_13(_10), .out_14(_11), .out_15(_12),
    .out_16(_13), .out_17(_14), .out_18(_15), .out_19(_16), .out_20(_17));
  A_32 a_32_3 (
    .in_1(in_1), .in_2(in_2[15:0]), .in_3(in_3[15:0]), .out_4(out_4), .out_5(out_5), .out_6(out_6),
    .out_7(out_7), .out_8(out_8), .out_9(out_9), .out_10(out_10), .out_11(out_11), .out_12(out_12),
    .out_13(out_13), .out_14(out_14), .out_15(out_15), .out_16(out_16), .out_17(out_17), .out_18(out_18),
    .out_19(out_19), .out_20(C));
  Multiplexer #(.enable("false")) multiplexer_1 (.in0(a_32_1_out_4), .in1(_1), .out(out_20), .sel(C));
  Multiplexer #(.enable("false")) multiplexer_2 (.in0(a_32_1_out_5), .in1(_2), .out(out_21), .sel(C));
  Multiplexer #(.enable("false")) multiplexer_3 (.in0(a_32_1_out_6), .in1(_3), .out(out_22), .sel(C));
  Multiplexer #(.enable("false")) multiplexer_4 (.in0(a_32_1_out_7), .in1(_4), .out(out_23), .sel(C));
  Multiplexer #(.enable("false")) multiplexer_5 (.in0(a_32_1_out_8), .in1(_5), .out(out_24), .sel(C));
  Multiplexer #(.enable("false")) multiplexer_6 (.in0(a_32_1_out_9), .in1(_6), .out(out_25), .sel(C));
  Multiplexer #(.enable("false")) multiplexer_7 (.in0(a_32_1_out_10), .in1(_7), .out(out_26), .sel(C));
  Multiplexer #(.enable("false")) multiplexer_8 (.in0(a_32_1_out_11), .in1(_8), .out(out_27), .sel(C));
  Multiplexer #(.enable("false")) multiplexer_9 (.in0(a_32_1_out_12), .in1(_9), .out(out_28), .sel(C));
  Multiplexer #(.enable("false")) multiplexer_10 (.in0(a_32_1_out_13), .in1(_10), .out(out_29), .sel(C));
  Multiplexer #(.enable("false")) multiplexer_11 (.in0(a_32_1_out_14), .in1(_11), .out(out_30), .sel(C));
  Multiplexer #(.enable("false")) multiplexer_12 (.in0(a_32_1_out_15), .in1(_12), .out(out_31), .sel(C));
  Multiplexer #(.enable("false")) multiplexer_13 (.in0(a_32_1_out_16), .in1(_13), .out(out_32), .sel(C));
  Multiplexer #(.enable("false")) multiplexer_14 (.in0(a_32_1_out_17), .in1(_14), .out(out_33), .sel(C));
  Multiplexer #(.enable("false")) multiplexer_15 (.in0(a_32_1_out_18), .in1(_15), .out(out_34), .sel(C));
  Multiplexer #(.enable("false")) multiplexer_16 (.in0(a_32_1_out_19), .in1(_16), .out(out_35), .sel(C));
  Multiplexer #(.enable("false")) multiplexer_17 (.in0(a_32_1_out_20), .in1(_17), .out(out_36), .sel(C));
endmodule

module Add_Sub (
  input  [31:0] in_1,
  input  [31:0] in_2,
  input  sub,
  output OVF,
  output NEG,
  output [31:0] out_6
);

  wire [31:0] addsubxor_1_out_3;

  S_Adder s_adder_1 (
    .A(in_1), .B(addsubxor_1_out_3), .C_0(sub), .Neg(NEG), .OVF(OVF), .out_7(out_6[31]), .out_8(out_6[30]),
    .out_9(out_6[29]), .out_10(out_6[28]), .out_11(out_6[27]), .out_12(out_6[26]), .out_13(out_6[25]),
    .out_14(out_6[24]), .out_15(out_6[23]), .out_16(out_6[22]), .out_17(out_6[21]), .out_18(out_6[20]),
    .out_19(out_6[19]), .out_20(out_6[18]), .out_21(out_6[17]), .out_22(out_6[16]), .out_23(out_6[15]),
    .out_24(out_6[14]), .out_25(out_6[13]), .out_26(out_6[12]), .out_27(out_6[11]), .out_28(out_6[10]),
    .out_29(out_6[9]), .out_30(out_6[8]), .out_31(out_6[7]), .out_32(out_6[6]), .out_33(out_6[5]),
    .out_34(out_6[4]), .out_35(out_6[3]), .out_36(out_6[2]), .out_37(out_6[1]), .out_38(out_6[0]));  // open: C_n
  AddSubXOR addsubxor_1 (.in_2(in_2), .out_3(addsubxor_1_out_3), .in_1(sub));
endmodule

module AddSubXOR (
  input  in_1,
  input  [31:0] in_2,
  output [31:0] out_3
);

  xor xor_1 (out_3[31], in_2[31], in_1);
  xor xor_2 (out_3[30], in_2[30], in_1);
  xor xor_3 (out_3[29], in_2[29], in_1);
  xor xor_4 (out_3[28], in_2[28], in_1);
  xor xor_5 (out_3[27], in_2[27], in_1);
  xor xor_6 (out_3[26], in_2[26], in_1);
  xor xor_7 (out_3[25], in_2[25], in_1);
  xor xor_8 (out_3[23], in_2[23], in_1);
  xor xor_9 (out_3[24], in_2[24], in_1);
  xor xor_10 (out_3[22], in_2[22], in_1);
  xor xor_11 (out_3[21], in_2[21], in_1);
  xor xor_12 (out_3[19], in_2[19], in_1);
  xor xor_13 (out_3[20], in_2[20], in_1);
  xor xor_14 (out_3[18], in_2[18], in_1);
  xor xor_15 (out_3[17], in_2[17], in_1);
  xor xor_16 (out_3[15], in_2[15], in_1);
  xor xor_17 (out_3[16], in_2[16], in_1);
  xor xor_18 (out_3[14], in_2[14], in_1);
  xor xor_19 (out_3[13], in_2[13], in_1);
  xor xor_20 (out_3[11], in_2[11], in_1);
  xor xor_21 (out_3[12], in_2[12], in_1);
  xor xor_22 (out_3[10], in_2[10], in_1);
  xor xor_23 (out_3[9], in_2[9], in_1);
  xor xor_24 (out_3[7], in_2[7], in_1);
  xor xor_25 (out_3[8], in_2[8], in_1);
  xor xor_26 (out_3[6], in_2[6], in_1);
  xor xor_27 (out_3[5], in_2[5], in_1);
  xor xor_28 (out_3[4], in_2[4], in_1);
  xor xor_29 (out_3[3], in_2[3], in_1);
  xor xor_30 (out_3[2], in_2[2], in_1);
  xor xor_31 (out_3[1], in_2[1], in_1);
  xor xor_32 (out_3[0], in_2[0], in_1);
endmodule

module Shifter (
  input  shift,
  input  right,
  input  [4:0] in_3,
  input  [31:0] in_4,
  output [31:0] out_5
);

  wire [31:0] shifter_1_out, shifter_2_out;

  Shifter_part #(.width(32)) shifter_1 (.in(in_4), .\dist (in_3), .out(shifter_1_out));
  Shifter_part #(.width(32), .shift("lr")) shifter_2 (.in(in_4), .\dist (in_3), .out(shifter_2_out));
  Multiplexer #(.select(2), .width(32), .enable("false")) multiplexer_1 (
    .in0(in_4), .in1(in_4), .in2(shifter_1_out), .in3(shifter_2_out), .out(out_5), .sel({shift, right}));
endmodule

module XOR32 (
  input  [31:0] B,
  input  [31:0] A,
  output [31:0] out_3
);

  xor xor_1 (out_3[31], A[31], B[31]);
  xor xor_2 (out_3[30], A[30], B[30]);
  xor xor_3 (out_3[29], A[29], B[29]);
  xor xor_4 (out_3[28], A[28], B[28]);
  xor xor_5 (out_3[26], A[26], B[26]);
  xor xor_6 (out_3[27], A[27], B[27]);
  xor xor_7 (out_3[25], A[25], B[25]);
  xor xor_8 (out_3[24], A[24], B[24]);
  xor xor_9 (out_3[22], A[22], B[22]);
  xor xor_10 (out_3[23], A[23], B[23]);
  xor xor_11 (out_3[21], A[21], B[21]);
  xor xor_12 (out_3[20], A[20], B[20]);
  xor xor_13 (out_3[18], A[18], B[18]);
  xor xor_14 (out_3[19], A[19], B[19]);
  xor xor_15 (out_3[17], A[17], B[17]);
  xor xor_16 (out_3[16], A[16], B[16]);
  xor xor_17 (out_3[14], A[14], B[14]);
  xor xor_18 (out_3[15], A[15], B[15]);
  xor xor_19 (out_3[13], A[13], B[13]);
  xor xor_20 (out_3[12], A[12], B[12]);
  xor xor_21 (out_3[10], A[10], B[10]);
  xor xor_22 (out_3[11], A[11], B[11]);
  xor xor_23 (out_3[9], A[9], B[9]);
  xor xor_24 (out_3[8], A[8], B[8]);
  xor xor_25 (out_3[6], A[6], B[6]);
  xor xor_26 (out_3[7], A[7], B[7]);
  xor xor_27 (out_3[5], A[5], B[5]);
  xor xor_28 (out_3[4], A[4], B[4]);
  xor xor_29 (out_3[2], A[2], B[2]);
  xor xor_30 (out_3[3], A[3], B[3]);
  xor xor_31 (out_3[1], A[1], B[1]);
  xor xor_32 (out_3[0], A[0], B[0]);
endmodule

module AND32 (
  input  [31:0] in_1,
  input  [31:0] in_2,
  output [31:0] out_3
);

  and and_1 (out_3[31], in_2[31], in_1[31]);
  and and_2 (out_3[30], in_2[30], in_1[30]);
  and and_3 (out_3[29], in_2[29], in_1[29]);
  and and_4 (out_3[28], in_2[28], in_1[28]);
  and and_5 (out_3[26], in_2[26], in_1[26]);
  and and_6 (out_3[27], in_2[27], in_1[27]);
  and and_7 (out_3[25], in_2[25], in_1[25]);
  and and_8 (out_3[24], in_2[24], in_1[24]);
  and and_9 (out_3[22], in_2[22], in_1[22]);
  and and_10 (out_3[23], in_2[23], in_1[23]);
  and and_11 (out_3[21], in_2[21], in_1[21]);
  and and_12 (out_3[20], in_2[20], in_1[20]);
  and and_13 (out_3[19], in_2[19], in_1[19]);
  and and_14 (out_3[18], in_2[18], in_1[18]);
  and and_15 (out_3[17], in_2[17], in_1[17]);
  and and_16 (out_3[16], in_2[16], in_1[16]);
  and and_17 (out_3[15], in_2[15], in_1[15]);
  and and_18 (out_3[14], in_2[14], in_1[14]);
  and and_19 (out_3[13], in_2[13], in_1[13]);
  and and_20 (out_3[12], in_2[12], in_1[12]);
  and and_21 (out_3[10], in_2[10], in_1[10]);
  and and_22 (out_3[11], in_2[11], in_1[11]);
  and and_23 (out_3[9], in_2[9], in_1[9]);
  and and_24 (out_3[8], in_2[8], in_1[8]);
  and and_25 (out_3[6], in_2[6], in_1[6]);
  and and_26 (out_3[7], in_2[7], in_1[7]);
  and and_27 (out_3[5], in_2[5], in_1[5]);
  and and_28 (out_3[4], in_2[4], in_1[4]);
  and and_29 (out_3[2], in_2[2], in_1[2]);
  and and_30 (out_3[3], in_2[3], in_1[3]);
  and and_31 (out_3[1], in_2[1], in_1[1]);
  and and_32 (out_3[0], in_2[0], in_1[0]);
endmodule

module OR32 (
  input  [31:0] in_1,
  input  [31:0] in_2,
  output [31:0] out_3
);

  or or_1 (out_3[31], in_2[31], in_1[31]);
  or or_2 (out_3[30], in_2[30], in_1[30]);
  or or_3 (out_3[29], in_2[29], in_1[29]);
  or or_4 (out_3[28], in_2[28], in_1[28]);
  or or_5 (out_3[26], in_2[26], in_1[26]);
  or or_6 (out_3[27], in_2[27], in_1[27]);
  or or_7 (out_3[25], in_2[25], in_1[25]);
  or or_8 (out_3[24], in_2[24], in_1[24]);
  or or_9 (out_3[23], in_2[23], in_1[23]);
  or or_10 (out_3[22], in_2[22], in_1[22]);
  or or_11 (out_3[21], in_2[21], in_1[21]);
  or or_12 (out_3[20], in_2[20], in_1[20]);
  or or_13 (out_3[19], in_2[19], in_1[19]);
  or or_14 (out_3[18], in_2[18], in_1[18]);
  or or_15 (out_3[17], in_2[17], in_1[17]);
  or or_16 (out_3[16], in_2[16], in_1[16]);
  or or_17 (out_3[14], in_2[14], in_1[14]);
  or or_18 (out_3[15], in_2[15], in_1[15]);
  or or_19 (out_3[13], in_2[13], in_1[13]);
  or or_20 (out_3[12], in_2[12], in_1[12]);
  or or_21 (out_3[10], in_2[10], in_1[10]);
  or or_22 (out_3[11], in_2[11], in_1[11]);
  or or_23 (out_3[9], in_2[9], in_1[9]);
  or or_24 (out_3[8], in_2[8], in_1[8]);
  or or_25 (out_3[7], in_2[7], in_1[7]);
  or or_26 (out_3[6], in_2[6], in_1[6]);
  or or_27 (out_3[5], in_2[5], in_1[5]);
  or or_28 (out_3[4], in_2[4], in_1[4]);
  or or_29 (out_3[2], in_2[2], in_1[2]);
  or or_30 (out_3[3], in_2[3], in_1[3]);
  or or_31 (out_3[1], in_2[1], in_1[1]);
  or or_32 (out_3[0], in_2[0], in_1[0]);
endmodule

module ALU (
  input  [4:0] in_1,
  input  [31:0] A,
  input  [31:0] B,
  output NEG,
  output OVF,
  output [31:0] out_6
);

  wire not_1_out, xor_1_out;
  wire [31:0] A_S, AND, OR, XOR;

  not not_1 (not_1_out, in_1[2]);
  xor xor_1 (xor_1_out, not_1_out, in_1[0]);
  Add_Sub Add_Sub (.in_1(A), .in_2(B), .sub(xor_1_out), .NEG(NEG), .OVF(OVF), .out_6(A_S));
  Multiplexer #(.select(5), .width(32), .enable("false")) multiplexer_1 (
    .in1(A_S), .in3(A_S), .in5(A_S), .in7(A_S), .in8(A_S), .in9(A_S), .in11(A_S), .in12(A_S), .in13(A_S),
    .in15(A_S), .in16(XOR), .in17(A_S), .in19(A_S), .in20(OR), .in21(A_S), .in23(A_S), .in24(AND),
    .in25(A_S), .in27(A_S), .in29(A_S), .in31(A_S), .out(out_6), .sel(in_1));  // open: in0, in2, in4, in6, in10, in14, in18, in22, in26, in28, in30
  XOR32 XOR_32 (.A(A), .out_3(XOR), .B(B));
  AND32 AND_32 (.in_2(A), .out_3(AND), .in_1(B));
  OR32 OR_32 (.in_2(A), .out_3(OR), .in_1(B));
endmodule
