// Logisim project Lab8.circ as structural Verilog
module Task1A (
);

  wire clock_1_out;
  wire [7:0] adder_1_out, register_1_q;

  Clock clock_1 (.out(clock_1_out));
  Register register_1 (.D(adder_1_out), .en(1'b1), .Q(register_1_q), .clk(clock_1_out));  // open: clr
  Hex_Digit_Display hex_digit_display_1 (.value(register_1_q[7:4]));  // open: dp
  Hex_Digit_Display hex_digit_display_2 (.value(register_1_q[3:0]));  // open: dp
  Adder adder_1 (.a(register_1_q), .b(8'h1), .out(adder_1_out));  // open: cin, cout
endmodule

module Task1B (
);

  wire clock_1_out;
  wire [7:0] adder_1_out, register_1_q;

  Register register_1 (.D(adder_1_out), .en(1'b1), .Q(register_1_q), .clk(clock_1_out));  // open: clr
  Clock clock_1 (.out(clock_1_out));
  Hex_Digit_Display hex_digit_display_1 (.value(register_1_q[3:0]));  // open: dp
  Hex_Digit_Display hex_digit_display_2 (.value(register_1_q[7:4]));  // open: dp
  Adder adder_1 (.a(register_1_q), .b({8{1'b1}}), .out(adder_1_out));  // open: cin, cout
endmodule

module Task1C (
);

  wire button_1_out, clock_1_out;
  wire [7:0] adder_1_out, multiplexer_1_out, register_1_q;

  Register register_1 (.D(adder_1_out), .en(1'b1), .Q(register_1_q), .clk(clock_1_out));  // open: clr
  Clock clock_1 (.out(clock_1_out));
  Multiplexer #(.width(8), .enable("false")) multiplexer_1 (
    .in0(8'h1), .in1({8{1'b1}}), .out(multiplexer_1_out), .sel(button_1_out));
  Hex_Digit_Display hex_digit_display_1 (.value(register_1_q[7:4]));  // open: dp
  Hex_Digit_Display hex_digit_display_2 (.value(register_1_q[3:0]));  // open: dp
  Adder adder_1 (.a(register_1_q), .b(multiplexer_1_out), .out(adder_1_out));  // open: cin, cout
  Button button_1 (.out(button_1_out));
endmodule

module Task2 (
);

  wire clock_1_out;
  wire [4:0] adder_1_out, register_1_q;
  wire [31:0] adder_2_out, parallelreadoutreg_1_out_4, parallelreadoutreg_1_out_5,
       parallelreadoutreg_1_out_6, parallelreadoutreg_1_out_7, parallelreadoutreg_1_out_8,
       parallelreadoutreg_1_out_9, parallelreadoutreg_1_out_10, parallelreadoutreg_1_out_11,
       parallelreadoutreg_1_out_12, parallelreadoutreg_1_out_13, parallelreadoutreg_1_out_14,
       parallelreadoutreg_1_out_15, parallelreadoutreg_1_out_16, parallelreadoutreg_1_out_17,
       parallelreadoutreg_1_out_18, parallelreadoutreg_1_out_19, parallelreadoutreg_1_out_20,
       parallelreadoutreg_1_out_21, parallelreadoutreg_1_out_22, parallelreadoutreg_1_out_23,
       parallelreadoutreg_1_out_24, parallelreadoutreg_1_out_25, parallelreadoutreg_1_out_26,
       parallelreadoutreg_1_out_27, parallelreadoutreg_1_out_28, parallelreadoutreg_1_out_29,
       parallelreadoutreg_1_out_30, parallelreadoutreg_1_out_31, parallelreadoutreg_1_out_32,
       parallelreadoutreg_1_out_33, parallelreadoutreg_1_out_34, parallelreadoutreg_1_out_35, register_2_q;

  Clock clock_1 (.out(clock_1_out));
  Register #(.width(5)) register_1 (.D(adder_1_out), .Q(register_1_q), .clk(clock_1_out));  // open: en, clr
  Register #(.width(32)) register_2 (.D(adder_2_out), .Q(register_2_q), .clk(clock_1_out));  // open: en, clr
  Adder #(.width(5)) adder_1 (.a(register_1_q), .b(5'b00001), .out(adder_1_out));  // open: cin, cout
  Adder #(.width(32)) adder_2 (.a(register_2_q), .b(32'h1), .out(adder_2_out));  // open: cin, cout
  DotMatrix #(.matrixcols(32), .matrixrows(32)) dotmatrix_1 (
    .col0(parallelreadoutreg_1_out_4), .col1(parallelreadoutreg_1_out_12),
    .col2(parallelreadoutreg_1_out_20), .col3(parallelreadoutreg_1_out_28),
    .col4(parallelreadoutreg_1_out_5), .col5(parallelreadoutreg_1_out_13),
    .col6(parallelreadoutreg_1_out_21), .col7(parallelreadoutreg_1_out_29),
    .col8(parallelreadoutreg_1_out_6), .col9(parallelreadoutreg_1_out_14),
    .col10(parallelreadoutreg_1_out_22), .col11(parallelreadoutreg_1_out_30),
    .col12(parallelreadoutreg_1_out_7), .col13(parallelreadoutreg_1_out_15),
    .col14(parallelreadoutreg_1_out_23), .col15(parallelreadoutreg_1_out_31),
    .col16(parallelreadoutreg_1_out_8), .col17(parallelreadoutreg_1_out_16),
    .col18(parallelreadoutreg_1_out_24), .col19(parallelreadoutreg_1_out_32),
    .col20(parallelreadoutreg_1_out_9), .col21(parallelreadoutreg_1_out_17),
    .col22(parallelreadoutreg_1_out_25), .col23(parallelreadoutreg_1_out_33),
    .col24(parallelreadoutreg_1_out_10), .col25(parallelreadoutreg_1_out_18),
    .col26(parallelreadoutreg_1_out_26), .col27(parallelreadoutreg_1_out_34),
    .col28(parallelreadoutreg_1_out_11), .col29(parallelreadoutreg_1_out_19),
    .col30(parallelreadoutreg_1_out_27), .col31(parallelreadoutreg_1_out_35));
  ParallelReadOutReg parallelreadoutreg_1 (
    .in_1(register_2_q), .in_2(clock_1_out), .in_3(register_1_q), .out_4(parallelreadoutreg_1_out_4),
    .out_12(parallelreadoutreg_1_out_12), .out_20(parallelreadoutreg_1_out_20),
    .out_28(parallelreadoutreg_1_out_28), .out_5(parallelreadoutreg_1_out_5),
    .out_13(parallelreadoutreg_1_out_13), .out_21(parallelreadoutreg_1_out_21),
    .out_29(parallelreadoutreg_1_out_29), .out_6(parallelreadoutreg_1_out_6),
    .out_14(parallelreadoutreg_1_out_14), .out_22(parallelreadoutreg_1_out_22),
    .out_30(parallelreadoutreg_1_out_30), .out_7(parallelreadoutreg_1_out_7),
    .out_15(parallelreadoutreg_1_out_15), .out_23(parallelreadoutreg_1_out_23),
    .out_31(parallelreadoutreg_1_out_31), .out_8(parallelreadoutreg_1_out_8),
    .out_16(parallelreadoutreg_1_out_16), .out_24(parallelreadoutreg_1_out_24),
    .out_32(parallelreadoutreg_1_out_32), .out_9(parallelreadoutreg_1_out_9),
    .out_17(parallelreadoutreg_1_out_17), .out_25(parallelreadoutreg_1_out_25),
    .out_33(parallelreadoutreg_1_out_33), .out_10(parallelreadoutreg_1_out_10),
    .out_18(parallelreadoutreg_1_out_18), .out_26(parallelreadoutreg_1_out_26),
    .out_34(parallelreadoutreg_1_out_34), .out_11(parallelreadoutreg_1_out_11),
    .out_19(parallelreadoutreg_1_out_19), .out_27(parallelreadoutreg_1_out_27),
    .out_35(parallelreadoutreg_1_out_35));  // open: out_36
endmodule

module ParallelReadOutReg (
  input  [31:0] in_1,
  input  in_2,
  input  [4:0] in_3,
  output [31:0] out_4,
  output [31:0] out_5,
  output [31:0] out_6,
  output [31:0] out_7,
  output [31:0] out_8,
  output [31:0] out_9,
  output [31:0] out_10,
  output [31:0] out_11,
  output [31:0] out_12,
  output [31:0] out_13,
  output [31:0] out_14,
  output [31:0] out_15,
  output [31:0] out_16,
  output [31:0] out_17,
  output [31:0] out_18,
  output [31:0] out_19,
  output [31:0] out_20,
  output [31:0] out_21,
  output [31:0] out_22,
  output [31:0] out_23,
  output [31:0] out_24,
  output [31:0] out_25,
  output [31:0] out_26,
  output [31:0] out_27,
  output [31:0] out_28,
  output [31:0] out_29,
  output [31:0] out_30,
  output [31:0] out_31,
  output [31:0] out_32,
  output [31:0] out_33,
  output [31:0] out_34,
  output [31:0] out_35,
  output [31:0] out_36
);

  wire decoder_1_out0, decoder_1_out1, decoder_1_out2, decoder_1_out3, decoder_1_out4, decoder_1_out5,
       decoder_1_out6, decoder_1_out7, decoder_1_out8, decoder_1_out9, decoder_1_out10, decoder_1_out11,
       decoder_1_out12, decoder_1_out13, decoder_1_out14, decoder_1_out15, decoder_1_out16, decoder_1_out17,
       decoder_1_out18, decoder_1_out19, decoder_1_out20, decoder_1_out21, decoder_1_out22, decoder_1_out23,
       decoder_1_out24, decoder_1_out25, decoder_1_out26, decoder_1_out27, decoder_1_out28, decoder_1_out29,
       decoder_1_out30, decoder_1_out31;

  Multiplexer #(.select(5), .width(32)) multiplexer_1 (
    .in0(out_4), .in1(out_12), .in2(out_20), .in3(out_28), .in4(out_5), .in5(out_13), .in6(out_21),
    .in7(out_29), .in8(out_6), .in9(out_14), .in10(out_22), .in11(out_30), .in12(out_7), .in13(out_15),
    .in14(out_23), .in15(out_31), .in16(out_8), .in17(out_16), .in18(out_24), .in19(out_32), .in20(out_9),
    .in21(out_17), .in22(out_25), .in23(out_33), .in24(out_10), .in25(out_18), .in26(out_26), .in27(out_34),
    .in28(out_11), .in29(out_19), .in30(out_27), .in31(out_35), .out(out_36), .sel(in_3));  // open: en
  Register #(.width(32)) register_1 (.D(in_1), .en(decoder_1_out0), .Q(out_4), .clk(in_2));  // open: clr
  Register #(.width(32)) register_2 (.D(in_1), .en(decoder_1_out1), .Q(out_12), .clk(in_2));  // open: clr
  Register #(.width(32)) register_3 (.D(in_1), .en(decoder_1_out2), .Q(out_20), .clk(in_2));  // open: clr
  Register #(.width(32)) register_4 (.D(in_1), .en(decoder_1_out3), .Q(out_28), .clk(in_2));  // open: clr
  Register #(.width(32)) register_5 (.D(in_1), .en(decoder_1_out4), .Q(out_5), .clk(in_2));  // open: clr
  Register #(.width(32)) register_6 (.D(in_1), .en(decoder_1_out5), .Q(out_13), .clk(in_2));  // open: clr
  Register #(.width(32)) register_7 (.D(in_1), .en(decoder_1_out6), .Q(out_21), .clk(in_2));  // open: clr
  Register #(.width(32)) register_8 (.D(in_1), .en(decoder_1_out7), .Q(out_29), .clk(in_2));  // open: clr
  Decoder #(.select(5)) decoder_1 (
    .out0(decoder_1_out0), .out1(decoder_1_out1), .out2(decoder_1_out2), .out3(decoder_1_out3),
    .out4(decoder_1_out4), .out5(decoder_1_out5), .out6(decoder_1_out6), .out7(decoder_1_out7),
    .out8(decoder_1_out8), .out9(decoder_1_out9), .out10(decoder_1_out10), .out11(decoder_1_out11),
    .out12(decoder_1_out12), .out13(decoder_1_out13), .out14(decoder_1_out14), .out15(decoder_1_out15),
    .out16(decoder_1_out16), .out17(decoder_1_out17), .out18(decoder_1_out18), .out19(decoder_1_out19),
    .out20(decoder_1_out20), .out21(decoder_1_out21), .out22(decoder_1_out22), .out23(decoder_1_out23),
    .out24(decoder_1_out24), .out25(decoder_1_out25), .out26(decoder_1_out26), .out27(decoder_1_out27),
    .out28(decoder_1_out28), .out29(decoder_1_out29), .out30(decoder_1_out30), .out31(decoder_1_out31),
    .sel(in_3));  // open: en
  Register #(.width(32)) register_9 (.D(in_1), .en(decoder_1_out8), .Q(out_6), .clk(in_2));  // open: clr
  Register #(.width(32)) register_10 (.D(in_1), .en(decoder_1_out9), .Q(out_14), .clk(in_2));  // open: clr
  Register #(.width(32)) register_11 (.D(in_1), .en(decoder_1_out10), .Q(out_22), .clk(in_2));  // open: clr
  Register #(.width(32)) register_12 (.D(in_1), .en(decoder_1_out11), .Q(out_30), .clk(in_2));  // open: clr
  Register #(.width(32)) register_13 (.D(in_1), .en(decoder_1_out12), .Q(out_7), .clk(in_2));  // open: clr
  Register #(.width(32)) register_14 (.D(in_1), .en(decoder_1_out13), .Q(out_15), .clk(in_2));  // open: clr
  Register #(.width(32)) register_15 (.D(in_1), .en(decoder_1_out14), .Q(out_23), .clk(in_2));  // open: clr
  Register #(.width(32)) register_16 (.D(in_1), .en(decoder_1_out15), .Q(out_31), .clk(in_2));  // open: clr
  Register #(.width(32)) register_17 (.D(in_1), .en(decoder_1_out16), .Q(out_8), .clk(in_2));  // open: clr
  Register #(.width(32)) register_18 (.D(in_1), .en(decoder_1_out17), .Q(out_16), .clk(in_2));  // open: clr
  Register #(.width(32)) register_19 (.D(in_1), .en(decoder_1_out18), .Q(out_24), .clk(in_2));  // open: clr
  Register #(.width(32)) register_20 (.D(in_1), .en(decoder_1_out19), .Q(out_32), .clk(in_2));  // open: clr
  Register #(.width(32)) register_21 (.D(in_1), .en(decoder_1_out20), .Q(out_9), .clk(in_2));  // open: clr
  Register #(.width(32)) register_22 (.D(in_1), .en(decoder_1_out21), .Q(out_17), .clk(in_2));  // open: clr
  Register #(.width(32)) register_23 (.D(in_1), .en(decoder_1_out22), .Q(out_25), .clk(in_2));  // open: clr
  Register #(.width(32)) register_24 (.D(in_1), .en(decoder_1_out23), .Q(out_33), .clk(in_2));  // open: clr
  Register #(.width(32)) register_25 (.D(in_1), .en(decoder_1_out24), .Q(out_10), .clk(in_2));  // open: clr
  Register #(.width(32)) register_26 (.D(in_1), .en(decoder_1_out25), .Q(out_18), .clk(in_2));  // open: clr
  Register #(.width(32)) register_27 (.D(in_1), .en(decoder_1_out26), .Q(out_26), .clk(in_2));  // open: clr
  Register #(.width(32)) register_28 (.D(in_1), .en(decoder_1_out27), .Q(out_34), .clk(in_2));  // open: clr
  Register #(.width(32)) register_29 (.D(in_1), .en(decoder_1_out28), .Q(out_11), .clk(in_2));  // open: clr
  Register #(.width(32)) register_30 (.D(in_1), .en(decoder_1_out29), .Q(out_19), .clk(in_2));  // open: clr
  Register #(.width(32)) register_31 (.D(in_1), .en(decoder_1_out30), .Q(out_27), .clk(in_2));  // open: clr
  Register #(.width(32)) register_32 (.D(in_1), .en(decoder_1_out31), .Q(out_35), .clk(in_2));  // open: clr
endmodule
