// Logisim project LAB10asstCOMPLETE_TetrisV2.circ as structural Verilog: 15 circuits, main circuit GPRenv
module ReadWriteRegister32 (
  input  [31:0] WriteData,
  input  Str,
  input  [4:0] WriteAddr,
  input  [4:0] ReadAddr,
  input  Clk,
  output [31:0] WriteDataOut,
  output [31:0] ReadData,
  output StrOut,
  output [4:0] WriteAddrOut,
  output ClkOut
);

  wire RI0, RI1, RI2, RI3, RI4, RI5, RI6, RI7, RI8, RI9, RI10, RI11, RI12, RI13, RI14, RI15, RI16, RI17,
       RI18, RI19, RI20, RI21, RI22, RI23, RI24, RI25, RI26, RI27, RI28, RI29, RI30, RI31;
  wire [31:0] RO0, RO1, RO2, RO3, RO4, RO5, RO6, RO7, RO8, RO9, RO10, RO11, RO12, RO13, RO14, RO15, RO16,
       RO17, RO18, RO19, RO20, RO21, RO22, RO23, RO24, RO25, RO26, RO27, RO28, RO29, RO30, RO31;

  Demultiplexer #(.select(5)) demultiplexer_1 (
    .out0(RI0), .out1(RI1), .out2(RI2), .out3(RI3), .out4(RI4), .out5(RI5), .out6(RI6), .out7(RI7),
    .out8(RI8), .out9(RI9), .out10(RI10), .out11(RI11), .out12(RI12), .out13(RI13), .out14(RI14),
    .out15(RI15), .out16(RI16), .out17(RI17), .out18(RI18), .out19(RI19), .out20(RI20), .out21(RI21),
    .out22(RI22), .out23(RI23), .out24(RI24), .out25(RI25), .out26(RI26), .out27(RI27), .out28(RI28),
    .out29(RI29), .out30(RI30), .out31(RI31), .in(Str), .sel(WriteAddr));  // open: en
  Register #(.width(32)) register_1 (.D(WriteData), .en(RI0), .Q(RO0), .clk(Clk));  // open: clr
  Register #(.width(32)) register_2 (.D(WriteData), .en(RI1), .Q(RO1), .clk(Clk));  // open: clr
  Register #(.width(32)) register_3 (.D(WriteData), .en(RI2), .Q(RO2), .clk(Clk));  // open: clr
  Register #(.width(32)) register_4 (.D(WriteData), .en(RI3), .Q(RO3), .clk(Clk));  // open: clr
  Register #(.width(32)) register_5 (.D(WriteData), .en(RI4), .Q(RO4), .clk(Clk));  // open: clr
  Register #(.width(32)) register_6 (.D(WriteData), .en(RI5), .Q(RO5), .clk(Clk));  // open: clr
  Register #(.width(32)) register_7 (.D(WriteData), .en(RI6), .Q(RO6), .clk(Clk));  // open: clr
  Register #(.width(32)) register_8 (.D(WriteData), .en(RI7), .Q(RO7), .clk(Clk));  // open: clr
  Register #(.width(32)) register_9 (.D(WriteData), .en(RI8), .Q(RO8), .clk(Clk));  // open: clr
  Register #(.width(32)) register_10 (.D(WriteData), .en(RI9), .Q(RO9), .clk(Clk));  // open: clr
  Register #(.width(32)) register_11 (.D(WriteData), .en(RI10), .Q(RO10), .clk(Clk));  // open: clr
  Register #(.width(32)) register_12 (.D(WriteData), .en(RI11), .Q(RO11), .clk(Clk));  // open: clr
  Register #(.width(32)) register_13 (.D(WriteData), .en(RI12), .Q(RO12), .clk(Clk));  // open: clr
  Register #(.width(32)) register_14 (.D(WriteData), .en(RI13), .Q(RO13), .clk(Clk));  // open: clr
  Register #(.width(32)) register_15 (.D(WriteData), .en(RI14), .Q(RO14), .clk(Clk));  // open: clr
  Register #(.width(32)) register_16 (.D(WriteData), .en(RI15), .Q(RO15), .clk(Clk));  // open: clr
  Register #(.width(32)) register_17 (.D(WriteData), .en(RI16), .Q(RO16), .clk(Clk));  // open: clr
  Register #(.width(32)) register_18 (.D(WriteData), .en(RI17), .Q(RO17), .clk(Clk));  // open: clr
  Register #(.width(32)) register_19 (.D(WriteData), .en(RI18), .Q(RO18), .clk(Clk));  // open: clr
  Register #(.width(32)) register_20 (.D(WriteData), .en(RI19), .Q(RO19), .clk(Clk));  // open: clr
  Register #(.width(32)) register_21 (.D(WriteData), .en(RI20), .Q(RO20), .clk(Clk));  // open: clr
  Register #(.width(32)) register_22 (.D(WriteData), .en(RI21), .Q(RO21), .clk(Clk));  // open: clr
  Register #(.width(32)) register_23 (.D(WriteData), .en(RI22), .Q(RO22), .clk(Clk));  // open: clr
  Register #(.width(32)) register_24 (.D(WriteData), .en(RI23), .Q(RO23), .clk(Clk));  // open: clr
  Register #(.width(32)) register_25 (.D(WriteData), .en(RI24), .Q(RO24), .clk(Clk));  // open: clr
  Register #(.width(32)) register_26 (.D(WriteData), .en(RI25), .Q(RO25), .clk(Clk));  // open: clr
  Register #(.width(32)) register_27 (.D(WriteData), .en(RI26), .Q(RO26), .clk(Clk));  // open: clr
  Register #(.width(32)) register_28 (.D(WriteData), .en(RI27), .Q(RO27), .clk(Clk));  // open: clr
  Register #(.width(32)) register_29 (.D(WriteData), .en(RI28), .Q(RO28), .clk(Clk));  // open: clr
  Register #(.width(32)) register_30 (.D(WriteData), .en(RI29), .Q(RO29), .clk(Clk));  // open: clr
  Register #(.width(32)) register_31 (.D(WriteData), .en(RI30), .Q(RO30), .clk(Clk));  // open: clr
  Register #(.width(32)) register_32 (.D(WriteData), .en(RI31), .Q(RO31), .clk(Clk));  // open: clr
  Multiplexer #(.select(5), .width(32), .enable("false")) multiplexer_1 (
    .in0(RO0), .in1(RO1), .in2(RO2), .in3(RO3), .in4(RO4), .in5(RO5), .in6(RO6), .in7(RO7), .in8(RO8),
    .in9(RO9), .in10(RO10), .in11(RO11), .in12(RO12), .in13(RO13), .in14(RO14), .in15(RO15), .in16(RO16),
    .in17(RO17), .in18(RO18), .in19(RO19), .in20(RO20), .in21(RO21), .in22(RO22), .in23(RO23), .in24(RO24),
    .in25(RO25), .in26(RO26), .in27(RO27), .in28(RO28), .in29(RO29), .in30(RO30), .in31(RO31),
    .out(ReadData), .sel(ReadAddr));

  assign ClkOut = Clk;
  assign StrOut = Str;
  assign WriteAddrOut = WriteAddr;
  assign WriteDataOut = WriteData;
endmodule

module GPRenv (
  input  CLK,
  input  [31:0] C,
  input  [4:0] Badr,
  input  [4:0] Aadr,
  input  [4:0] Cadr,
  input  GPR_WE,
  output ClkOut,
  output [31:0] Cout,
  output [31:0] B,
  output [31:0] A,
  output [4:0] CadrOut,
  output AEQZ,
  output GPR_WE_out
);

  wire and_1_out, or_1_out, readwriteregister32_1_clkout, readwriteregister32_1_strout,
       readwriteregister32_2_clkout, readwriteregister32_2_strout;
  wire [4:0] readwriteregister32_1_writeaddrout, readwriteregister32_2_writeaddrout;
  wire [31:0] readwriteregister32_1_writedataout, readwriteregister32_2_writedataout;

  or or_1 (or_1_out, Cadr[0], Cadr[1], Cadr[2], Cadr[3], Cadr[4]);
  and and_1 (and_1_out, or_1_out, GPR_WE);
  ReadWriteRegister32 readwriteregister32_1 (
    .WriteAddr(Cadr), .ReadAddr(Badr), .Clk(CLK), .ReadData(B), .Str(and_1_out), .WriteData(C),
    .WriteDataOut(readwriteregister32_1_writedataout), .StrOut(readwriteregister32_1_strout),
    .WriteAddrOut(readwriteregister32_1_writeaddrout), .ClkOut(readwriteregister32_1_clkout));
  RAM #(.addrWidth(5), .dataWidth(32), .bus("separate")) ram_1 (
    .addr(readwriteregister32_1_writeaddrout), .din(readwriteregister32_1_writedataout),
    .str(readwriteregister32_1_strout), .clk(readwriteregister32_1_clkout));  // open: data, sel, ld, clr
  ReadWriteRegister32 readwriteregister32_2 (
    .WriteAddr(Cadr), .ReadAddr(Aadr), .Clk(CLK), .ReadData(A), .Str(and_1_out), .WriteData(C),
    .WriteDataOut(readwriteregister32_2_writedataout), .StrOut(readwriteregister32_2_strout),
    .WriteAddrOut(readwriteregister32_2_writeaddrout), .ClkOut(readwriteregister32_2_clkout));
  RAM #(.addrWidth(5), .dataWidth(32), .bus("separate")) ram_2 (
    .addr(readwriteregister32_2_writeaddrout), .din(readwriteregister32_2_writedataout),
    .str(readwriteregister32_2_strout), .clk(readwriteregister32_2_clkout));  // open: data, sel, ld, clr
  Comparator #(.width(32), .mode("unsigned")) comparator_1 (.a(A), .b({32{1'b0}}), .eq(AEQZ));  // open: gt, lt

  assign CadrOut = Cadr;
  assign ClkOut = CLK;
  assign Cout = C;
  assign GPR_WE_out = GPR_WE;
endmodule

module IRenv (
  input  [31:0] DI,
  output [31:0] Inst,
  output [5:0] \function ,
  output JAL,
  output [4:0] Cadr,
  output [4:0] Badr,
  output [4:0] Aadr,
  output [5:0] opcode,
  output [31:0] Imm
);

  wire comparator_1_eq, not_1_out;
  wire [4:0] multiplexer_1_out;

  Comparator #(.width(6), .mode("unsigned")) comparator_1 (
    .a({6{1'b0}}), .b(DI[31:26]), .eq(comparator_1_eq));  // open: gt, lt
  not not_1 (not_1_out, comparator_1_eq);
  Multiplexer #(.width(5), .enable("false")) multiplexer_1 (
    .in0(DI[15:11]), .in1(DI[20:16]), .out(multiplexer_1_out), .sel(not_1_out));
  assign Imm = {{16{DI[15]}}, DI[15:0]};  // Bit_Extender bit_extender_1
  and and_1 (JAL, DI[28], DI[27], DI[26]);
  Multiplexer #(.width(5), .enable("false")) multiplexer_2 (
    .in0(multiplexer_1_out), .in1({5{1'b1}}), .out(Cadr), .sel(JAL));

  assign Aadr = DI[25:21];
  assign Badr = DI[20:16];
  assign \function  = DI[5:0];
  assign Inst = DI;
  assign opcode = DI[31:26];
endmodule

module MEMenv (
  input  [31:0] IN,
  input  [31:0] ADDRESS,
  input  [31:0] MDO,
  input  MW,
  input  MR,
  input  CLK,
  output [31:0] MDI,
  output [11:0] MA,
  output [31:0] OUT,
  output strO,
  output ldO,
  output clkO
);


  assign clkO = CLK;
  assign ldO = MR;
  assign MA = ADDRESS[11:0];
  assign MDI = IN;
  assign OUT = MDO;
  assign strO = MW;
endmodule

module MEMenv2 (
  input  [31:0] in_1,
  input  [31:0] IN,
  input  [31:0] ADDRESS,
  input  MW,
  input  MR,
  input  CLK,
  input  [1:0] Xcoord,
  input  [1:0] Ycoord,
  output [31:0] out_9,
  output out_10,
  output out_11,
  output out_12,
  output [15:0] out_13,
  output [31:0] OUT,
  output [31:0] out_15,
  output [4:0] out_16,
  output out_17,
  output out_18,
  output [3:0] HEXlow,
  output [3:0] HEXhigh
);

  wire and_2_out, comparator_1_eq, comparator_2_eq, comparator_3_eq, comparator_4_eq, comparator_5_eq,
       or_2_out;
  wire [1:0] and_5_out, and_6_out, bit_extender_1_out, bit_extender_2_out, register_1_q, register_2_q;
  wire [31:0] bit_extender_3_out, bit_extender_4_out, or_1_out;

  Comparator #(.width(27), .mode("unsigned")) comparator_1 (
    .a(ADDRESS[31:5]), .b(27'h80), .eq(comparator_1_eq));  // open: gt, lt
  Comparator #(.width(32), .mode("unsigned")) comparator_2 (
    .a(ADDRESS), .b(32'h2000), .eq(comparator_2_eq));  // open: gt, lt
  Comparator #(.width(32), .mode("unsigned")) comparator_3 (
    .a(ADDRESS), .b(32'h2001), .eq(comparator_3_eq));  // open: gt, lt
  Comparator #(.width(32), .mode("unsigned")) comparator_4 (
    .a(ADDRESS), .b(32'h3000), .eq(comparator_4_eq));  // open: gt, lt
  Comparator #(.width(16), .mode("unsigned")) comparator_5 (
    .a(ADDRESS[31:16]), .b({16{1'b0}}), .eq(comparator_5_eq));  // open: gt, lt
  and and_1 (out_18, comparator_1_eq, MW);
  Register #(.width(2)) register_1 (.D(Xcoord), .Q(register_1_q), .clk(CLK));  // open: en, clr
  assign bit_extender_1_out = {{1{comparator_2_eq}}, comparator_2_eq};  // Bit_Extender bit_extender_1
  Register #(.width(2)) register_2 (.D(Ycoord), .Q(register_2_q), .clk(CLK));  // open: en, clr
  assign bit_extender_2_out = {{1{comparator_3_eq}}, comparator_3_eq};  // Bit_Extender bit_extender_2
  and and_2 (and_2_out, MW, comparator_4_eq);
  and and_3 (out_10, comparator_5_eq, MW);
  and and_4 (out_12, comparator_5_eq, MR);
  assign bit_extender_3_out = {{30{1'b0}}, and_5_out};  // Bit_Extender bit_extender_3
  assign and_5_out = register_1_q & bit_extender_1_out;  // AND_Gate and_5, 2 bits wide
  assign and_6_out = register_2_q & bit_extender_2_out;  // AND_Gate and_6, 2 bits wide
  assign bit_extender_4_out = {{30{1'b0}}, and_6_out};  // Bit_Extender bit_extender_4
  Register register_3 (.D(IN[7:0]), .en(and_2_out), .Q({HEXhigh, HEXlow}), .clk(CLK));  // open: clr
  assign or_1_out = bit_extender_3_out | bit_extender_4_out;  // OR_Gate or_1, 32 bits wide
  or or_2 (or_2_out, comparator_2_eq, comparator_3_eq);
  Multiplexer #(.width(32), .enable("false")) multiplexer_1 (.in0(in_1), .in1(or_1_out), .out(OUT), .sel(or_2_out));

  assign out_9 = IN;
  assign out_11 = CLK;
  assign out_13 = ADDRESS[15:0];
  assign out_15 = IN;
  assign out_16 = ADDRESS[4:0];
  assign out_17 = CLK;
endmodule

module Add_Sub (
  input  sub,
  input  [31:0] A,
  input  [31:0] B,
  output [31:0] s,
  output ovf,
  output neg
);

  wire adder_1_cout, adder_2_cout;
  wire [31:0] bit_extender_1_out, xor_1_out;

  // Probe on bit_extender_1_out
  assign bit_extender_1_out = {{31{sub}}, sub};  // Bit_Extender bit_extender_1
  assign xor_1_out = bit_extender_1_out ^ B;  // XOR_Gate xor_1, 32 bits wide
  Adder #(.width(31)) adder_1 (.a(A[30:0]), .b(xor_1_out[30:0]), .out(s[30:0]), .cin(sub), .cout(adder_1_cout));
  Adder #(.width(1)) adder_2 (.a(A[31]), .b(xor_1_out[31]), .out(s[31]), .cin(adder_1_cout), .cout(adder_2_cout));
  xor xor_2 (ovf, adder_2_cout, adder_1_cout);
  ExactlyOne xor_3 (.out(neg), .in0(adder_2_cout), .in1(A[31]), .in2(xor_1_out[31]));
endmodule

module Logic (
  input  [31:0] A,
  input  [31:0] B,
  input  Ctrl_0,
  input  Ctrl_1,
  output [31:0] s
);

  wire [31:0] and_1_out, multiplexer_1_out, or_1_out, xor_1_out;

  assign xor_1_out = A ^ B;  // XOR_Gate xor_1, 32 bits wide
  assign or_1_out = A | B;  // OR_Gate or_1, 32 bits wide
  assign and_1_out = A & B;  // AND_Gate and_1, 32 bits wide
  Multiplexer #(.width(32), .enable("false")) multiplexer_1 (
    .in0(xor_1_out), .in1(or_1_out), .out(multiplexer_1_out), .sel(Ctrl_0));
  Multiplexer #(.width(32), .enable("false")) multiplexer_2 (
    .in0(multiplexer_1_out), .in1(and_1_out), .out(s), .sel(Ctrl_1));
endmodule

module Comp (
  input  Cntr_0,
  input  Cntr_1,
  input  Cntr_2,
  input  [31:0] isum,
  input  neg,
  output [31:0] s
);

  wire and_1_out, and_2_out, and_3_out, comparator_1_eq, nor_1_out, or_1_out;

  Comparator #(.width(32), .mode("unsigned")) comparator_1 (
    .a({32{1'b0}}), .b(isum), .eq(comparator_1_eq));  // open: gt, lt
  nor nor_1 (nor_1_out, neg, comparator_1_eq);
  and and_1 (and_1_out, Cntr_0, nor_1_out);
  and and_2 (and_2_out, Cntr_1, comparator_1_eq);
  and and_3 (and_3_out, Cntr_2, neg);
  or or_1 (or_1_out, and_1_out, and_2_out);
  or or_2 (s[0], or_1_out, and_3_out);

  assign s[31:1] = {31{1'b0}};
endmodule

module ALU (
  input  [4:0] \type ,
  input  [31:0] X,
  input  [31:0] Y,
  output [31:0] Z
);

  wire add_sub_1_neg;
  wire [31:0] add_sub_1_s, comp_1_s, logic_1_s, multiplexer_1_out;

  Logic logic_1 (.A(X), .B(Y), .Ctrl_0(\type [2]), .Ctrl_1(\type [3]), .s(logic_1_s));
  Comp comp_1 (
    .Cntr_0(\type [2]), .Cntr_1(\type [3]), .Cntr_2(\type [4]), .isum(add_sub_1_s), .neg(add_sub_1_neg),
    .s(comp_1_s));
  Add_Sub add_sub_1 (.sub(\type [1]), .A(X), .B(Y), .s(add_sub_1_s), .neg(add_sub_1_neg));  // open: ovf
  Multiplexer #(.width(32), .enable("false")) multiplexer_1 (
    .in0(logic_1_s), .in1(comp_1_s), .out(multiplexer_1_out), .sel(\type [1]));
  Multiplexer #(.width(32), .enable("false")) multiplexer_2 (
    .in0(multiplexer_1_out), .in1(add_sub_1_s), .out(Z), .sel(\type [0]));
endmodule

module Shifter (
  input  [31:0] X,
  input  right,
  input  shift,
  output [31:0] Z
);

  wire [31:0] multiplexer_2_out, shifter_1_out, shifter_2_out;

  Shifter_part #(.width(32)) shifter_1 (.in(X), .\dist (5'b00001), .out(shifter_1_out));
  Shifter_part #(.width(32), .shift("lr")) shifter_2 (.in(X), .\dist (5'b00001), .out(shifter_2_out));
  Multiplexer #(.width(32), .enable("false")) multiplexer_1 (.in0(X), .in1(multiplexer_2_out), .out(Z), .sel(shift));
  Multiplexer #(.width(32), .enable("false")) multiplexer_2 (
    .in0(shifter_1_out), .in1(shifter_2_out), .out(multiplexer_2_out), .sel(right));
endmodule

module SingleCycleDLX (
  input  Clk
);

  wire beqz, bnez, branch, bsel, btaken, clock_1_out, Csel, DINTsel, GPR_WE, gprenv_1_aeqz, gprenv_1_clkout,
       gprenv_1_gpr_we_out, irenv_1_jal, Itype, ji, jr, memenv_1_clko, memenv_1_ldo, memenv_1_stro, MR, MW,
       right, Rtype, shift, sub, type_0, type_1;
  wire [1:0] not_2_out;
  wire [2:0] type_4_2;
  wire [4:0] db3, gprenv_1_cadrout, irenv_1_aadr, irenv_1_badr, irenv_1_cadr;
  wire [5:0] irenv_1_function, irenv_1_opcode;
  wire [11:0] memenv_1_ma;
  wire [31:0] adder_1_out, adder_2_out, db1, db2, db4, gprenv_1_b, gprenv_1_cout, irenv_1_imm, mem2use_1_out,
       memenv_1_mdi, memenv_1_out, multiplexer_1_out, multiplexer_2_out, multiplexer_3_out,
       multiplexer_6_out, multiplexer_7_out, ram_1_data, register_1_q, shifter_1_z;

  Register #(.width(32)) register_1 (.D(multiplexer_3_out), .Q(register_1_q), .clk(clock_1_out));  // open: en, clr
  Clock clock_1 (.out(clock_1_out));
  Adder #(.width(32)) adder_1 (.a(32'h1), .b(register_1_q), .out(adder_1_out));  // open: cin, cout
  MEMenv memenv_1 (
    .IN({32{1'b0}}), .ADDRESS(register_1_q), .MW(1'b0), .MR(1'b1), .OUT(memenv_1_out), .CLK(clock_1_out),
    .MA(memenv_1_ma), .MDO(ram_1_data), .clkO(memenv_1_clko), .MDI(memenv_1_mdi), .strO(memenv_1_stro),
    .ldO(memenv_1_ldo));
  // Probe on adder_1_out
  // Probe on memenv_1_out
  // Probe on irenv_1_imm
  IRenv irenv_1 (
    .DI(memenv_1_out), .\function (irenv_1_function), .Cadr(irenv_1_cadr), .Badr(irenv_1_badr),
    .Aadr(irenv_1_aadr), .opcode(irenv_1_opcode), .Imm(irenv_1_imm), .JAL(irenv_1_jal));  // open: Inst
  RAM #(.addrWidth(12), .dataWidth(32), .bus("separate")) ram_1 (
    .addr(memenv_1_ma), .din(memenv_1_mdi), .data(ram_1_data), .str(memenv_1_stro), .clk(memenv_1_clko),
    .ld(memenv_1_ldo));  // open: sel, clr
  // Probe on multiplexer_3_out
  Control control_1 (
    .Opcode(irenv_1_opcode), .Function(irenv_1_function), .AEQZ(gprenv_1_aeqz), .Btaken(btaken),
    .branch(branch), .bnez(bnez), .ji(ji), .jr(jr), .Bsel(bsel), .MW(MW), .MR(MR), .Csel(Csel),
    .GPR_WE(GPR_WE), .Itype(Itype), .Rtype(Rtype), .type_4_2(type_4_2), .type_1(type_1), .type_0(type_0),
    .shift(shift), .right(right), .DINTsel(DINTsel), .sub(sub), .beqz(beqz));
  Adder #(.width(32)) adder_2 (.a(adder_1_out), .b(irenv_1_imm), .out(adder_2_out));  // open: cin, cout
  Multiplexer #(.width(32), .enable("false")) multiplexer_1 (
    .in0(multiplexer_7_out), .in1(adder_1_out), .out(multiplexer_1_out), .sel(irenv_1_jal));
  GPRenv gprenv_1 (
    .C(multiplexer_1_out), .CLK(clock_1_out), .GPR_WE(GPR_WE), .Cadr(irenv_1_cadr), .Aadr(irenv_1_aadr),
    .Badr(irenv_1_badr), .A(db1), .B(gprenv_1_b), .AEQZ(gprenv_1_aeqz), .ClkOut(gprenv_1_clkout),
    .Cout(gprenv_1_cout), .GPR_WE_out(gprenv_1_gpr_we_out), .CadrOut(gprenv_1_cadrout));
  // Probe on gprenv_1_b
  Multiplexer #(.width(32), .enable("false")) multiplexer_2 (
    .in0(adder_1_out), .in1(adder_2_out), .out(multiplexer_2_out), .sel(btaken));
  RAM #(.addrWidth(5), .dataWidth(32), .bus("separate")) ram_2 (
    .addr(gprenv_1_cadrout), .din(gprenv_1_cout), .str(gprenv_1_gpr_we_out), .clk(gprenv_1_clkout));  // open: data, sel, ld, clr
  // Probe on db1
  Multiplexer #(.width(32), .enable("false")) multiplexer_3 (
    .in0(multiplexer_2_out), .in1(db1), .out(multiplexer_3_out), .sel(jr));
  Multiplexer #(.width(32), .enable("false")) multiplexer_4 (
    .in0(gprenv_1_b), .in1(irenv_1_imm), .out(db4), .sel(bsel));
  Multiplexer #(.width(5), .enable("false")) multiplexer_5 (
    .in0({type_4_2, type_1, type_0}), .in1({type_4_2, not_2_out}), .out(db3), .sel(sub));
  not not_1 (not_2_out[1], type_1);
  not not_2 (not_2_out[0], type_0);
  Lab_9_ALU ALU (.A(db1), .B(db4), .out_6(db2), .in_1(db3));  // open: NEG, OVF
  Shifter shifter_1 (.X(db1), .right(right), .shift(shift), .Z(shifter_1_z));
  // Probe on db1
  // Probe on db4
  // Probe on multiplexer_6_out
  Multiplexer #(.width(32), .enable("false")) multiplexer_6 (
    .in0(db2), .in1(shifter_1_z), .out(multiplexer_6_out), .sel(DINTsel));
  Multiplexer #(.width(32), .enable("false")) multiplexer_7 (
    .in0(multiplexer_6_out), .in1(mem2use_1_out), .out(multiplexer_7_out), .sel(Csel));
  // Probe on db2
  // Probe on db3
  // Probe on multiplexer_7_out
  MEM2use mem2use_1 (
    .CLK(clock_1_out), .IN(gprenv_1_b), .ADDRESS(multiplexer_6_out), .MW(MW), .MR(MR), .OUT(mem2use_1_out));

  // Notes on the sheet:
  //   PC
  //   Instruction
  //   memory
  //   IR
  //   env
  //   opcode
  //   function
  //   AEQZ
  //   GPR_WE
  //   type[4:0]
  //   btaken
  //   Bsel
  //   jr
  //   shift
  //   right
  //   DINTsel
  //   MW
  //   MR
  //   Csel
endmodule

module Control (
  input  [5:0] Opcode,
  input  [5:0] Function,
  input  AEQZ,
  output Btaken,
  output branch,
  output bnez,
  output ji,
  output jr,
  output Bsel,
  output MW,
  output MR,
  output Csel,
  output GPR_WE,
  output Itype,
  output Rtype,
  output [2:0] type_4_2,
  output type_1,
  output type_0,
  output shift,
  output right,
  output DINTsel,
  output sub,
  output beqz
);

  wire add, addi, addsubandorxor, \and , and_2_out, and_6_out, and_12_out, and_14_out, jali, jalr, ji_t,
       jr_t, jump_branch, not_1_out, not_2_out, not_3_out, not_4_out, not_5_out, not_6_out, not_7_out,
       not_8_out, not_9_out, not_11_out, \or , s, seqi, sgei, sgti, slei, sll, slti, snei, srl, \xor ,
       xor_1_out;

  not not_1 (not_1_out, Opcode[5]);
  and and_1 (s, not_1_out, and_2_out);
  and and_2 (and_2_out, Opcode[4], Opcode[3]);
  Demultiplexer #(.select(3), .enable("false")) demultiplexer_1 (
    .out1(sgti), .out2(seqi), .out3(sgei), .out4(slti), .out5(snei), .out6(slei), .in(s), .sel(Opcode[2:0]));  // open: out0, out7
  not not_2 (not_2_out, Opcode[5]);
  not not_3 (not_3_out, Opcode[4]);
  and and_3 (addi, not_2_out, not_3_out, Opcode[3], not_4_out, Opcode[1], Opcode[0]);
  not not_4 (not_4_out, Opcode[2]);
  and and_4 (MW, Opcode[5], Opcode[3]);
  and and_5 (Csel, Opcode[5], not_5_out);
  not not_5 (not_5_out, Opcode[3]);
  not not_6 (not_6_out, Opcode[3]);
  and and_6 (and_6_out, not_6_out, Opcode[2]);
  not not_7 (not_7_out, Opcode[5]);
  and and_7 (jump_branch, not_7_out, and_6_out);
  nor nor_1 (Rtype, Opcode[5], Opcode[4], Opcode[3], Opcode[2], Opcode[1], Opcode[0]);
  not not_8 (not_8_out, Function[5]);
  Demultiplexer #(.select(3), .enable("false")) demultiplexer_2 (
    .out0(beqz), .out1(bnez), .out2(ji_t), .out3(jali), .out6(jr_t), .out7(jalr), .in(jump_branch),
    .sel({Opcode[4], Opcode[1:0]}));  // open: out4, out5
  and and_8 (DINTsel, Rtype, not_8_out);
  and and_9 (addsubandorxor, Rtype, Function[5]);
  Demultiplexer #(.select(3), .enable("false")) demultiplexer_3 (
    .out2(sub), .out3(add), .out4(\xor ), .out5(\or ), .out6(\and ), .in(addsubandorxor), .sel(Function[2:0]));  // open: out0, out1, out7
  and and_10 (sll, DINTsel, not_9_out);
  not not_9 (not_9_out, Function[1]);
  and and_11 (srl, DINTsel, Function[1]);
  or or_1 (branch, beqz, bnez, ji_t, jali);
  not not_10 (Bsel, Rtype);
  not not_11 (not_11_out, Opcode[5]);
  and and_12 (and_12_out, not_11_out, Opcode[4], Opcode[3]);
  xor xor_1 (xor_1_out, AEQZ, bnez);
  Multiplexer #(.width(3), .enable("false")) multiplexer_1 (
    .in0(Function[2:0]), .in1(Opcode[2:0]), .out(type_4_2), .sel(s));
  or or_2 (type_1, and_12_out, sub);
  or or_3 (type_0, MW, Csel, addi, add, sub);
  and and_13 (right, DINTsel, srl);
  or or_4 (Btaken, ji_t, and_14_out);
  and and_14 (and_14_out, branch, xor_1_out);
  or or_5 (ji, ji_t, jali);
  or or_6 (jr, jr_t, jalr);
  or or_7 (GPR_WE, Csel, Rtype, s, addi, jali, jalr);

  assign Itype = Bsel;
  assign MR = Csel;
  assign shift = DINTsel;

  // Other names for the same wires on the sheet: _29 = Opcode[3]; _31 = Opcode[5]; lw_sw = Opcode[5]; _30 = Opcode[4];
  //   _0 = Function[0]; _1 = Function[1]; _2 = Function[2]; _26 = Opcode[0]; _27 = Opcode[1]; _28 = Opcode[2];
  //   _3 = Function[3]; _4 = Function[4]; _5 = Function[5]; lw = Csel; Opcode_0 = Rtype; sw = MW
endmodule

module _32bitwiseAND (
  input  in_1,
  input  in_2,
  input  in_3,
  input  in_4,
  input  in_5,
  input  in_6,
  input  in_7,
  input  in_8,
  input  in_9,
  input  in_10,
  input  in_11,
  input  in_12,
  input  in_13,
  input  in_14,
  input  in_15,
  input  in_16,
  input  enable,
  input  in_18,
  input  in_19,
  input  in_20,
  input  in_21,
  input  in_22,
  input  in_23,
  input  in_24,
  input  in_25,
  input  in_26,
  input  in_27,
  input  in_28,
  input  in_29,
  input  in_30,
  input  in_31,
  input  in_32,
  input  in_33,
  output out_34,
  output out_35,
  output out_36,
  output out_37,
  output out_38,
  output out_39,
  output out_40,
  output out_41,
  output out_42,
  output out_43,
  output out_44,
  output out_45,
  output out_46,
  output out_47,
  output out_48,
  output out_49,
  output out_50,
  output out_51,
  output out_52,
  output out_53,
  output out_54,
  output out_55,
  output out_56,
  output out_57,
  output out_58,
  output out_59,
  output out_60,
  output out_61,
  output out_62,
  output out_63,
  output out_64,
  output out_65
);

  wire [31:0] bit_extender_1_out;

  assign bit_extender_1_out = {{31{enable}}, enable};  // Bit_Extender bit_extender_1
  assign {out_50, out_34, out_51, out_35, out_52, out_36, out_53, out_37, out_54, out_38, out_55, out_39, out_56, out_40, out_57, out_41, out_58, out_42, out_59, out_43, out_60, out_44, out_61, out_45, out_62, out_46, out_63, out_47, out_64, out_48, out_65, out_49} = bit_extender_1_out & {in_1, in_18, in_2, in_19, in_3, in_20, in_4, in_21, in_5, in_22, in_6, in_23, in_7, in_24, in_8, in_25, in_9, in_26, in_10, in_27, in_11, in_28, in_12, in_29, in_13, in_30, in_14, in_31, in_15, in_32, in_16, in_33};  // AND_Gate and_1, 32 bits wide
endmodule

module ParallelReadOutReg (
  input  [31:0] in_1,
  input  in_2,
  input  Enable,
  input  [4:0] in_4,
  output [31:0] out_5,
  output [31:0] out_6,
  output [31:0] out_7,
  output [31:0] out_8,
  output [31:0] out_9,
  output [31:0] out_10,
  output [31:0] out_11,
  output [31:0] out_12,
  output [31:0] out_13,
  output [31:0] out_14,
  output [31:0] out_15,
  output [31:0] out_16,
  output [31:0] out_17,
  output [31:0] out_18,
  output [31:0] out_19,
  output [31:0] out_20,
  output [31:0] out_21,
  output [31:0] out_22,
  output [31:0] out_23,
  output [31:0] out_24,
  output [31:0] out_25,
  output [31:0] out_26,
  output [31:0] out_27,
  output [31:0] out_28,
  output [31:0] out_29,
  output [31:0] out_30,
  output [31:0] out_31,
  output [31:0] out_32,
  output [31:0] out_33,
  output [31:0] out_34,
  output [31:0] out_35,
  output [31:0] out_36,
  output [31:0] out_37
);

  wire decoder_1_out0, decoder_1_out1, decoder_1_out2, decoder_1_out3, decoder_1_out4, decoder_1_out5,
       decoder_1_out6, decoder_1_out7, decoder_1_out8, decoder_1_out9, decoder_1_out10, decoder_1_out11,
       decoder_1_out12, decoder_1_out13, decoder_1_out14, decoder_1_out15, decoder_1_out16, decoder_1_out17,
       decoder_1_out18, decoder_1_out19, decoder_1_out20, decoder_1_out21, decoder_1_out22, decoder_1_out23,
       decoder_1_out24, decoder_1_out25, decoder_1_out26, decoder_1_out27, decoder_1_out28, decoder_1_out29,
       decoder_1_out30, decoder_1_out31, n32bitwiseand_1_out_34, n32bitwiseand_1_out_35,
       n32bitwiseand_1_out_36, n32bitwiseand_1_out_37, n32bitwiseand_1_out_38, n32bitwiseand_1_out_39,
       n32bitwiseand_1_out_40, n32bitwiseand_1_out_41, n32bitwiseand_1_out_42, n32bitwiseand_1_out_43,
       n32bitwiseand_1_out_44, n32bitwiseand_1_out_45, n32bitwiseand_1_out_46, n32bitwiseand_1_out_47,
       n32bitwiseand_1_out_48, n32bitwiseand_1_out_49, n32bitwiseand_1_out_50, n32bitwiseand_1_out_51,
       n32bitwiseand_1_out_52, n32bitwiseand_1_out_53, n32bitwiseand_1_out_54, n32bitwiseand_1_out_55,
       n32bitwiseand_1_out_56, n32bitwiseand_1_out_57, n32bitwiseand_1_out_58, n32bitwiseand_1_out_59,
       n32bitwiseand_1_out_60, n32bitwiseand_1_out_61, n32bitwiseand_1_out_62, n32bitwiseand_1_out_63,
       n32bitwiseand_1_out_64, n32bitwiseand_1_out_65;

  Multiplexer #(.select(5), .width(32)) multiplexer_1 (
    .in0(out_5), .in1(out_13), .in2(out_21), .in3(out_29), .in4(out_6), .in5(out_14), .in6(out_22),
    .in7(out_30), .in8(out_7), .in9(out_15), .in10(out_23), .in11(out_31), .in12(out_8), .in13(out_16),
    .in14(out_24), .in15(out_32), .in16(out_9), .in17(out_17), .in18(out_25), .in19(out_33), .in20(out_10),
    .in21(out_18), .in22(out_26), .in23(out_34), .in24(out_11), .in25(out_19), .in26(out_27), .in27(out_35),
    .in28(out_12), .in29(out_20), .in30(out_28), .in31(out_36), .out(out_37), .sel(in_4));  // open: en
  Register #(.width(32)) register_1 (.D(in_1), .en(n32bitwiseand_1_out_50), .Q(out_5), .clk(in_2));  // open: clr
  Register #(.width(32)) register_2 (.D(in_1), .en(n32bitwiseand_1_out_34), .Q(out_13), .clk(in_2));  // open: clr
  Register #(.width(32)) register_3 (.D(in_1), .en(n32bitwiseand_1_out_51), .Q(out_21), .clk(in_2));  // open: clr
  Register #(.width(32)) register_4 (.D(in_1), .en(n32bitwiseand_1_out_35), .Q(out_29), .clk(in_2));  // open: clr
  Register #(.width(32)) register_5 (.D(in_1), .en(n32bitwiseand_1_out_52), .Q(out_6), .clk(in_2));  // open: clr
  Register #(.width(32)) register_6 (.D(in_1), .en(n32bitwiseand_1_out_36), .Q(out_14), .clk(in_2));  // open: clr
  Register #(.width(32)) register_7 (.D(in_1), .en(n32bitwiseand_1_out_53), .Q(out_22), .clk(in_2));  // open: clr
  Register #(.width(32)) register_8 (.D(in_1), .en(n32bitwiseand_1_out_37), .Q(out_30), .clk(in_2));  // open: clr
  Decoder #(.select(5)) decoder_1 (
    .out0(decoder_1_out0), .out1(decoder_1_out1), .out2(decoder_1_out2), .out3(decoder_1_out3),
    .out4(decoder_1_out4), .out5(decoder_1_out5), .out6(decoder_1_out6), .out7(decoder_1_out7),
    .out8(decoder_1_out8), .out9(decoder_1_out9), .out10(decoder_1_out10), .out11(decoder_1_out11),
    .out12(decoder_1_out12), .out13(decoder_1_out13), .out14(decoder_1_out14), .out15(decoder_1_out15),
    .out16(decoder_1_out16), .out17(decoder_1_out17), .out18(decoder_1_out18), .out19(decoder_1_out19),
    .out20(decoder_1_out20), .out21(decoder_1_out21), .out22(decoder_1_out22), .out23(decoder_1_out23),
    .out24(decoder_1_out24), .out25(decoder_1_out25), .out26(decoder_1_out26), .out27(decoder_1_out27),
    .out28(decoder_1_out28), .out29(decoder_1_out29), .out30(decoder_1_out30), .out31(decoder_1_out31),
    .sel(in_4));  // open: en
  Register #(.width(32)) register_9 (.D(in_1), .en(n32bitwiseand_1_out_54), .Q(out_7), .clk(in_2));  // open: clr
  Register #(.width(32)) register_10 (.D(in_1), .en(n32bitwiseand_1_out_38), .Q(out_15), .clk(in_2));  // open: clr
  Register #(.width(32)) register_11 (.D(in_1), .en(n32bitwiseand_1_out_55), .Q(out_23), .clk(in_2));  // open: clr
  Register #(.width(32)) register_12 (.D(in_1), .en(n32bitwiseand_1_out_39), .Q(out_31), .clk(in_2));  // open: clr
  Register #(.width(32)) register_13 (.D(in_1), .en(n32bitwiseand_1_out_56), .Q(out_8), .clk(in_2));  // open: clr
  Register #(.width(32)) register_14 (.D(in_1), .en(n32bitwiseand_1_out_40), .Q(out_16), .clk(in_2));  // open: clr
  Register #(.width(32)) register_15 (.D(in_1), .en(n32bitwiseand_1_out_57), .Q(out_24), .clk(in_2));  // open: clr
  Register #(.width(32)) register_16 (.D(in_1), .en(n32bitwiseand_1_out_41), .Q(out_32), .clk(in_2));  // open: clr
  Register #(.width(32)) register_17 (.D(in_1), .en(n32bitwiseand_1_out_58), .Q(out_9), .clk(in_2));  // open: clr
  Register #(.width(32)) register_18 (.D(in_1), .en(n32bitwiseand_1_out_42), .Q(out_17), .clk(in_2));  // open: clr
  Register #(.width(32)) register_19 (.D(in_1), .en(n32bitwiseand_1_out_59), .Q(out_25), .clk(in_2));  // open: clr
  Register #(.width(32)) register_20 (.D(in_1), .en(n32bitwiseand_1_out_43), .Q(out_33), .clk(in_2));  // open: clr
  _32bitwiseAND u_32bitwiseand_1 (
    .out_50(n32bitwiseand_1_out_50), .out_34(n32bitwiseand_1_out_34), .out_51(n32bitwiseand_1_out_51),
    .out_35(n32bitwiseand_1_out_35), .out_52(n32bitwiseand_1_out_52), .out_36(n32bitwiseand_1_out_36),
    .out_53(n32bitwiseand_1_out_53), .out_37(n32bitwiseand_1_out_37), .out_54(n32bitwiseand_1_out_54),
    .out_38(n32bitwiseand_1_out_38), .out_55(n32bitwiseand_1_out_55), .out_39(n32bitwiseand_1_out_39),
    .out_56(n32bitwiseand_1_out_56), .out_40(n32bitwiseand_1_out_40), .out_57(n32bitwiseand_1_out_57),
    .out_41(n32bitwiseand_1_out_41), .out_58(n32bitwiseand_1_out_58), .out_42(n32bitwiseand_1_out_42),
    .out_59(n32bitwiseand_1_out_59), .out_43(n32bitwiseand_1_out_43), .out_60(n32bitwiseand_1_out_60),
    .out_44(n32bitwiseand_1_out_44), .out_61(n32bitwiseand_1_out_61), .out_45(n32bitwiseand_1_out_45),
    .out_62(n32bitwiseand_1_out_62), .out_46(n32bitwiseand_1_out_46), .out_63(n32bitwiseand_1_out_63),
    .out_47(n32bitwiseand_1_out_47), .out_64(n32bitwiseand_1_out_64), .out_48(n32bitwiseand_1_out_48),
    .out_65(n32bitwiseand_1_out_65), .out_49(n32bitwiseand_1_out_49), .enable(Enable), .in_1(decoder_1_out0),
    .in_18(decoder_1_out1), .in_2(decoder_1_out2), .in_19(decoder_1_out3), .in_3(decoder_1_out4),
    .in_20(decoder_1_out5), .in_4(decoder_1_out6), .in_21(decoder_1_out7), .in_5(decoder_1_out8),
    .in_22(decoder_1_out9), .in_6(decoder_1_out10), .in_23(decoder_1_out11), .in_7(decoder_1_out12),
    .in_24(decoder_1_out13), .in_8(decoder_1_out14), .in_25(decoder_1_out15), .in_9(decoder_1_out16),
    .in_26(decoder_1_out17), .in_10(decoder_1_out18), .in_27(decoder_1_out19), .in_11(decoder_1_out20),
    .in_28(decoder_1_out21), .in_12(decoder_1_out22), .in_29(decoder_1_out23), .in_13(decoder_1_out24),
    .in_30(decoder_1_out25), .in_14(decoder_1_out26), .in_31(decoder_1_out27), .in_15(decoder_1_out28),
    .in_32(decoder_1_out29), .in_16(decoder_1_out30), .in_33(decoder_1_out31));
  Register #(.width(32)) register_21 (.D(in_1), .en(n32bitwiseand_1_out_60), .Q(out_10), .clk(in_2));  // open: clr
  Register #(.width(32)) register_22 (.D(in_1), .en(n32bitwiseand_1_out_44), .Q(out_18), .clk(in_2));  // open: clr
  Register #(.width(32)) register_23 (.D(in_1), .en(n32bitwiseand_1_out_61), .Q(out_26), .clk(in_2));  // open: clr
  Register #(.width(32)) register_24 (.D(in_1), .en(n32bitwiseand_1_out_45), .Q(out_34), .clk(in_2));  // open: clr
  Register #(.width(32)) register_25 (.D(in_1), .en(n32bitwiseand_1_out_62), .Q(out_11), .clk(in_2));  // open: clr
  Register #(.width(32)) register_26 (.D(in_1), .en(n32bitwiseand_1_out_46), .Q(out_19), .clk(in_2));  // open: clr
  Register #(.width(32)) register_27 (.D(in_1), .en(n32bitwiseand_1_out_63), .Q(out_27), .clk(in_2));  // open: clr
  Register #(.width(32)) register_28 (.D(in_1), .en(n32bitwiseand_1_out_47), .Q(out_35), .clk(in_2));  // open: clr
  Register #(.width(32)) register_29 (.D(in_1), .en(n32bitwiseand_1_out_64), .Q(out_12), .clk(in_2));  // open: clr
  Register #(.width(32)) register_30 (.D(in_1), .en(n32bitwiseand_1_out_48), .Q(out_20), .clk(in_2));  // open: clr
  Register #(.width(32)) register_31 (.D(in_1), .en(n32bitwiseand_1_out_65), .Q(out_28), .clk(in_2));  // open: clr
  Register #(.width(32)) register_32 (.D(in_1), .en(n32bitwiseand_1_out_49), .Q(out_36), .clk(in_2));  // open: clr
endmodule

module MEM2use (
  input  CLK,
  input  [31:0] IN,
  input  [31:0] ADDRESS,
  input  MW,
  input  MR,
  output [31:0] OUT
);

  wire clock_1_out, memenv2_1_out_10, memenv2_1_out_11, memenv2_1_out_12, memenv2_1_out_17, memenv2_1_out_18;
  wire [1:0] joystick_1_x, joystick_1_y;
  wire [3:0] memenv2_1_hexhigh, memenv2_1_hexlow;
  wire [4:0] memenv2_1_out_16;
  wire [15:0] memenv2_1_out_13;
  wire [31:0] memenv2_1_out_9, memenv2_1_out_15, parallelreadoutreg_1_out_5, parallelreadoutreg_1_out_6,
       parallelreadoutreg_1_out_7, parallelreadoutreg_1_out_8, parallelreadoutreg_1_out_9,
       parallelreadoutreg_1_out_10, parallelreadoutreg_1_out_11, parallelreadoutreg_1_out_12,
       parallelreadoutreg_1_out_13, parallelreadoutreg_1_out_14, parallelreadoutreg_1_out_15,
       parallelreadoutreg_1_out_16, parallelreadoutreg_1_out_17, parallelreadoutreg_1_out_18,
       parallelreadoutreg_1_out_19, parallelreadoutreg_1_out_20, parallelreadoutreg_1_out_21,
       parallelreadoutreg_1_out_22, parallelreadoutreg_1_out_23, parallelreadoutreg_1_out_24,
       parallelreadoutreg_1_out_25, parallelreadoutreg_1_out_26, parallelreadoutreg_1_out_27,
       parallelreadoutreg_1_out_28, parallelreadoutreg_1_out_29, parallelreadoutreg_1_out_30,
       parallelreadoutreg_1_out_31, parallelreadoutreg_1_out_32, parallelreadoutreg_1_out_33,
       parallelreadoutreg_1_out_34, parallelreadoutreg_1_out_35, parallelreadoutreg_1_out_36, ram_1_data;

  Clock clock_1 (.out(clock_1_out));
  Hex_Digit_Display hex_digit_display_1 (.value(memenv2_1_hexhigh));  // open: dp
  MEMenv2 memenv2_1 (
    .IN(IN), .ADDRESS(ADDRESS), .MW(MW), .MR(MR), .CLK(clock_1_out), .OUT(OUT), .out_15(memenv2_1_out_15),
    .out_16(memenv2_1_out_16), .out_17(memenv2_1_out_17), .out_18(memenv2_1_out_18), .Ycoord(joystick_1_y),
    .HEXlow(memenv2_1_hexlow), .HEXhigh(memenv2_1_hexhigh), .out_13(memenv2_1_out_13),
    .out_9(memenv2_1_out_9), .out_10(memenv2_1_out_10), .out_11(memenv2_1_out_11), .out_12(memenv2_1_out_12),
    .in_1(ram_1_data), .Xcoord(joystick_1_x));
  Hex_Digit_Display hex_digit_display_2 (.value(memenv2_1_hexlow));  // open: dp
  RAM #(.addrWidth(16), .dataWidth(32), .bus("separate")) ram_1 (
    .addr(memenv2_1_out_13), .din(memenv2_1_out_9), .data(ram_1_data), .str(memenv2_1_out_10),
    .clk(memenv2_1_out_11), .ld(memenv2_1_out_12));  // open: sel, clr
  // Probe on joystick_1_y
  // Probe on joystick_1_x
  Joystick #(.bits(2)) joystick_1 (.x(joystick_1_x), .y(joystick_1_y));
  DotMatrix #(.inputtype("row"), .matrixcols(32), .matrixrows(32)) dotmatrix_1 (
    .row0(parallelreadoutreg_1_out_5), .row1(parallelreadoutreg_1_out_13),
    .row2(parallelreadoutreg_1_out_21), .row3(parallelreadoutreg_1_out_29),
    .row4(parallelreadoutreg_1_out_6), .row5(parallelreadoutreg_1_out_14),
    .row6(parallelreadoutreg_1_out_22), .row7(parallelreadoutreg_1_out_30),
    .row8(parallelreadoutreg_1_out_7), .row9(parallelreadoutreg_1_out_15),
    .row10(parallelreadoutreg_1_out_23), .row11(parallelreadoutreg_1_out_31),
    .row12(parallelreadoutreg_1_out_8), .row13(parallelreadoutreg_1_out_16),
    .row14(parallelreadoutreg_1_out_24), .row15(parallelreadoutreg_1_out_32),
    .row16(parallelreadoutreg_1_out_9), .row17(parallelreadoutreg_1_out_17),
    .row18(parallelreadoutreg_1_out_25), .row19(parallelreadoutreg_1_out_33),
    .row20(parallelreadoutreg_1_out_10), .row21(parallelreadoutreg_1_out_18),
    .row22(parallelreadoutreg_1_out_26), .row23(parallelreadoutreg_1_out_34),
    .row24(parallelreadoutreg_1_out_11), .row25(parallelreadoutreg_1_out_19),
    .row26(parallelreadoutreg_1_out_27), .row27(parallelreadoutreg_1_out_35),
    .row28(parallelreadoutreg_1_out_12), .row29(parallelreadoutreg_1_out_20),
    .row30(parallelreadoutreg_1_out_28), .row31(parallelreadoutreg_1_out_36));
  ParallelReadOutReg parallelreadoutreg_1 (
    .in_1(memenv2_1_out_15), .in_2(memenv2_1_out_17), .Enable(memenv2_1_out_18), .in_4(memenv2_1_out_16),
    .out_5(parallelreadoutreg_1_out_5), .out_6(parallelreadoutreg_1_out_6),
    .out_7(parallelreadoutreg_1_out_7), .out_8(parallelreadoutreg_1_out_8),
    .out_9(parallelreadoutreg_1_out_9), .out_10(parallelreadoutreg_1_out_10),
    .out_11(parallelreadoutreg_1_out_11), .out_12(parallelreadoutreg_1_out_12),
    .out_13(parallelreadoutreg_1_out_13), .out_14(parallelreadoutreg_1_out_14),
    .out_15(parallelreadoutreg_1_out_15), .out_16(parallelreadoutreg_1_out_16),
    .out_17(parallelreadoutreg_1_out_17), .out_18(parallelreadoutreg_1_out_18),
    .out_19(parallelreadoutreg_1_out_19), .out_20(parallelreadoutreg_1_out_20),
    .out_21(parallelreadoutreg_1_out_21), .out_29(parallelreadoutreg_1_out_29),
    .out_22(parallelreadoutreg_1_out_22), .out_30(parallelreadoutreg_1_out_30),
    .out_23(parallelreadoutreg_1_out_23), .out_31(parallelreadoutreg_1_out_31),
    .out_24(parallelreadoutreg_1_out_24), .out_32(parallelreadoutreg_1_out_32),
    .out_25(parallelreadoutreg_1_out_25), .out_33(parallelreadoutreg_1_out_33),
    .out_26(parallelreadoutreg_1_out_26), .out_34(parallelreadoutreg_1_out_34),
    .out_27(parallelreadoutreg_1_out_27), .out_35(parallelreadoutreg_1_out_35),
    .out_28(parallelreadoutreg_1_out_28), .out_36(parallelreadoutreg_1_out_36));  // open: out_37
endmodule
